// Logisim project fish.circ as structural Verilog: 9 circuits, main circuit main
module main (
  output [15:0] out_1,
  output [15:0] out_2,
  output [15:0] out_3,
  output [15:0] out_4,
  output [15:0] out_5,
  output [15:0] out_6,
  output [15:0] out_7,
  output [15:0] out_8
);

  wire CLK;
  wire [3:0] ALUOP;
  wire [9:0] ADDR_OUT;
  wire [12:0] DATA_IN;
  wire [15:0] ALU_RESULT, multiplexer_1_out, multiplexer_2_out;

  RAM #(.addrWidth(10), .dataWidth(13), .bus("separate")) ram_1 (
    .addr(ADDR_OUT), .data({DATA_IN[12:10], ALUOP, DATA_IN[5:0]}), .clk(CLK));  // open: din, str, sel, ld, clr
  Clock clock_1 (.out(CLK));
  Register_Bank register_bank_1 (
    .REG_SELECT(DATA_IN[12:10]), .CLK(CLK), .OUT_1(out_2), .OUT_0(out_1), .OUT_2(out_3), .OUT_3(out_4),
    .OUT_4(out_5), .OUT_5(out_6), .OUT_6(out_7), .OUT_7(out_8), .REG_LOAD(1'b1), .IN(ALU_RESULT));
  Multiplexer #(.select(3), .width(16), .enable("false")) multiplexer_1 (
    .in0(out_1), .in1(out_2), .in2(out_3), .in3(out_4), .in4(out_5), .in5(out_6), .in6(out_7), .in7(out_8),
    .out(multiplexer_1_out), .sel(DATA_IN[2:0]));
  ALU alu_1 (.IN_0(multiplexer_1_out), .IN_1(multiplexer_2_out), .RESULT(ALU_RESULT), .ALUOP(ALUOP));
  Multiplexer #(.select(3), .width(16), .enable("false")) multiplexer_2 (
    .in0(out_1), .in1(out_2), .in2(out_3), .in3(out_4), .in4(out_5), .in5(out_6), .in6(out_7), .in7(out_8),
    .out(multiplexer_2_out), .sel(DATA_IN[5:3]));
  Program_Counter program_counter_1 (.PCINC(1'b1), .PCLD(1'b0), .CLK(CLK), .ADDR(ADDR_OUT));

  // Other names for the same wires on the sheet: SRC_1[2:0] = DATA_IN[2:0]; SRC_2[2:0] = DATA_IN[5:3];
  //   DATA_IN[9:6] = ALUOP; DST[2:0] = DATA_IN[12:10]; REG_0[15:0] = out_1; REG_1[15:0] = out_2; REG_2[15:0] = out_3;
  //   REG_3[15:0] = out_4; REG_4[15:0] = out_5; REG_5[15:0] = out_6; REG_6[15:0] = out_7; REG_7[15:0] = out_8
endmodule

module Register_Bank (
  input  REG_LOAD,
  input  [2:0] REG_SELECT,
  input  [15:0] IN,
  input  CLK,
  output [15:0] OUT_0,
  output [15:0] OUT_1,
  output [15:0] OUT_2,
  output [15:0] OUT_3,
  output [15:0] OUT_4,
  output [15:0] OUT_5,
  output [15:0] OUT_6,
  output [15:0] OUT_7
);

  wire decoder_1_out0, decoder_1_out1, decoder_1_out2, decoder_1_out3, decoder_1_out4, decoder_1_out5,
       decoder_1_out6, decoder_1_out7;

  Decoder #(.select(3), .disabled(0)) decoder_1 (
    .out0(decoder_1_out0), .out1(decoder_1_out1), .out2(decoder_1_out2), .out3(decoder_1_out3),
    .out4(decoder_1_out4), .out5(decoder_1_out5), .out6(decoder_1_out6), .out7(decoder_1_out7),
    .sel(REG_SELECT), .en(REG_LOAD));
  _16_bit_register u_16_bit_register_1 (.IN(IN), .LD(decoder_1_out0), .CLK(CLK), .OUT(OUT_0));
  _16_bit_register u_16_bit_register_2 (.IN(IN), .LD(decoder_1_out1), .CLK(CLK), .OUT(OUT_1));
  _16_bit_register u_16_bit_register_3 (.IN(IN), .LD(decoder_1_out2), .CLK(CLK), .OUT(OUT_2));
  _16_bit_register u_16_bit_register_4 (.IN(IN), .LD(decoder_1_out3), .CLK(CLK), .OUT(OUT_3));
  _16_bit_register u_16_bit_register_5 (.IN(IN), .LD(decoder_1_out4), .CLK(CLK), .OUT(OUT_4));
  _16_bit_register u_16_bit_register_6 (.IN(IN), .LD(decoder_1_out5), .CLK(CLK), .OUT(OUT_5));
  _16_bit_register u_16_bit_register_7 (.IN(IN), .LD(decoder_1_out6), .CLK(CLK), .OUT(OUT_6));
  _16_bit_register u_16_bit_register_8 (.IN(IN), .LD(decoder_1_out7), .CLK(CLK), .OUT(OUT_7));
endmodule

module ALU (
  input  [15:0] IN_0,
  input  [15:0] IN_1,
  input  [3:0] ALUOP,
  output [15:0] RESULT
);

  wire [15:0] adder_1_out, adder_2_out, and_1_out, Bitwise_Or_out, Bitwise_Xor_out, not_1_out,
       subtractor_1_out, subtractor_2_out;

  Adder #(.width(16)) adder_1 (.a(IN_0), .b(IN_1), .out(adder_1_out));  // open: cin, cout
  Subtractor #(.width(16)) subtractor_1 (.a(IN_0), .b(IN_1), .out(subtractor_1_out));  // open: bin, bout
  assign and_1_out = IN_0 & IN_1;  // AND_Gate and_1, 16 bits wide
  assign Bitwise_Or_out = IN_0 | IN_1;  // OR_Gate Bitwise_Or, 16 bits wide
  assign Bitwise_Xor_out = IN_0 ^ IN_1;  // XOR_Gate Bitwise_Xor, 16 bits wide
  assign not_1_out = ~IN_1;  // NOT_Gate not_1, 16 bits wide
  Adder #(.width(16)) adder_2 (.a(IN_1), .b(16'h1), .out(adder_2_out));  // open: cin, cout
  Subtractor #(.width(16)) subtractor_2 (.a(IN_1), .b(16'h1), .out(subtractor_2_out));  // open: bin, bout
  Multiplexer #(.select(4), .width(16), .enable("false")) multiplexer_1 (
    .in0(adder_1_out), .in1(subtractor_1_out), .in2(and_1_out), .in3(Bitwise_Or_out), .in4(Bitwise_Xor_out),
    .in5(not_1_out), .in6(IN_1), .in7(adder_2_out), .in8(subtractor_2_out), .out(RESULT), .sel(ALUOP));  // open: in9, in10, in11, in12, in13, in14, in15
endmodule

module _1_bit_register (
  input  DATA_IN,
  input  CLK,
  input  LOAD,
  output DATA_OUT
);

  wire not_1_out;

  not not_1 (not_1_out, DATA_IN);
  S_R_Flip_Flop s_r_ff_1 (.S(DATA_IN), .clk(CLK), .R(not_1_out), .Q(DATA_OUT), .en(LOAD));  // open: Qn, preset, reset
endmodule

module _16_bit_register (
  input  [15:0] IN,
  input  LD,
  input  CLK,
  output [15:0] OUT
);

  _4_bit_register u_4_bit_register_1 (.IN(IN[3:0]), .LD(LD), .CLK(CLK), .OUT(OUT[3:0]));
  _4_bit_register u_4_bit_register_2 (.IN(IN[7:4]), .LD(LD), .CLK(CLK), .OUT(OUT[7:4]));
  _4_bit_register u_4_bit_register_3 (.IN(IN[11:8]), .LD(LD), .CLK(CLK), .OUT(OUT[11:8]));
  _4_bit_register u_4_bit_register_4 (.IN(IN[15:12]), .LD(LD), .CLK(CLK), .OUT(OUT[15:12]));
endmodule

module _4_bit_register (
  input  [3:0] IN,
  input  LD,
  input  CLK,
  output [3:0] OUT
);

  _1_bit_register u_1_bit_register_1 (.DATA_IN(IN[0]), .CLK(CLK), .LOAD(LD), .DATA_OUT(OUT[0]));
  _1_bit_register u_1_bit_register_2 (.DATA_IN(IN[1]), .CLK(CLK), .LOAD(LD), .DATA_OUT(OUT[1]));
  _1_bit_register u_1_bit_register_3 (.DATA_IN(IN[2]), .CLK(CLK), .LOAD(LD), .DATA_OUT(OUT[2]));
  _1_bit_register u_1_bit_register_4 (.DATA_IN(IN[3]), .CLK(CLK), .LOAD(LD), .DATA_OUT(OUT[3]));
endmodule

module _10_bit_register (
  input  [9:0] IN,
  input  LD,
  input  CLK,
  output [9:0] OUT
);

  _4_bit_register u_4_bit_register_1 (.IN(IN[3:0]), .LD(LD), .CLK(CLK), .OUT(OUT[3:0]));
  _4_bit_register u_4_bit_register_2 (.IN(IN[7:4]), .LD(LD), .CLK(CLK), .OUT(OUT[7:4]));
  _1_bit_register u_1_bit_register_1 (.DATA_IN(IN[8]), .CLK(CLK), .LOAD(LD), .DATA_OUT(OUT[8]));
  _1_bit_register u_1_bit_register_2 (.DATA_IN(IN[9]), .CLK(CLK), .LOAD(LD), .DATA_OUT(OUT[9]));
endmodule

module Counter (
  input  [9:0] IN,
  input  PCINC,
  input  PCLD,
  input  CLK,
  output [9:0] OUT
);

  wire Bitwise_Or_out;
  wire [9:0] adder_1_out, multiplexer_1_out;

  Adder #(.width(10)) adder_1 (.a(OUT), .b(10'h1), .out(adder_1_out));  // open: cin, cout
  Multiplexer #(.width(10), .enable("false")) multiplexer_1 (
    .in0(IN), .in1(adder_1_out), .out(multiplexer_1_out), .sel(PCINC));
  or Bitwise_Or (Bitwise_Or_out, PCINC, PCLD);
  _10_bit_register u_10_bit_register_1 (.IN(multiplexer_1_out), .LD(Bitwise_Or_out), .CLK(CLK), .OUT(OUT));
endmodule

module Program_Counter (
  input  PCINC,
  input  PCLD,
  input  CLK,
  output [9:0] ADDR
);

  Counter counter_1 (.PCINC(PCINC), .PCLD(PCLD), .CLK(CLK), .OUT(ADDR));  // open: IN
endmodule
