// Logisim project reptile_8.circ as structural Verilog: 12 circuits, main circuit main
module main (
);

  wire alu_1_zf, ARMUX, CLK, IRLD, MEMLD, MUX, PCINC, PCLD, REGLD, ZF, ZFLD;
  wire [2:0] REG_1, REG_2, REG_3;
  wire [5:0] ALUOP;
  wire [11:0] OFFSET, program_counter_1_addr;
  wire [15:0] aaaa, ALU_RESULT, INSTRUCTION, multiplexer_1_out, multiplexer_3_out, register_bank_1_out_0,
       register_bank_1_out_1, register_bank_1_out_2, register_bank_1_out_3, register_bank_1_out_4,
       register_bank_1_out_5, register_bank_1_out_6, register_bank_1_out_7;

  Clock clock_1 (.out(CLK));
  Multiplexer #(.width(16), .enable("false")) multiplexer_1 (
    .in0(ALU_RESULT), .in1(INSTRUCTION), .out(multiplexer_1_out), .sel(MUX));
  Register_Bank register_bank_1 (
    .REG_SELECT(REG_1), .CLK(CLK), .OUT_1(register_bank_1_out_1), .OUT_0(register_bank_1_out_0),
    .OUT_2(register_bank_1_out_2), .OUT_3(register_bank_1_out_3), .OUT_4(register_bank_1_out_4),
    .OUT_5(register_bank_1_out_5), .OUT_6(register_bank_1_out_6), .OUT_7(register_bank_1_out_7),
    .REG_LOAD(REGLD), .IN(multiplexer_1_out));
  Instructor_Register instructor_register_1 (
    .IN(INSTRUCTION[11:0]), .CLK(CLK), .LD(IRLD), .OUT(OFFSET), .DST(REG_1), .SRC2(REG_3), .SRC1(REG_2),
    .ALUOP(ALUOP));
  Hex_Digit_Display hex_digit_display_1 (.value(register_bank_1_out_0[15:12]));  // open: dp
  Hex_Digit_Display hex_digit_display_2 (.value(register_bank_1_out_0[7:4]));  // open: dp
  Hex_Digit_Display hex_digit_display_3 (.value(register_bank_1_out_0[11:8]));  // open: dp
  Multiplexer #(.select(3), .width(16), .enable("false")) multiplexer_2 (
    .in0(register_bank_1_out_0), .in1(register_bank_1_out_1), .in2(register_bank_1_out_2),
    .in3(register_bank_1_out_3), .in4(register_bank_1_out_4), .in5(register_bank_1_out_5),
    .in6(register_bank_1_out_6), .in7(register_bank_1_out_7), .out(aaaa), .sel(REG_2));
  Hex_Digit_Display hex_digit_display_4 (.value(register_bank_1_out_0[3:0]));  // open: dp
  ALU alu_1 (.IN_0(aaaa), .IN_1(multiplexer_3_out), .RESULT(ALU_RESULT), .ZF(alu_1_zf), .ALUOP(ALUOP));
  Multiplexer #(.select(3), .width(16), .enable("false")) multiplexer_3 (
    .in0(register_bank_1_out_0), .in1(register_bank_1_out_1), .in2(register_bank_1_out_2),
    .in3(register_bank_1_out_3), .in4(register_bank_1_out_4), .in5(register_bank_1_out_5),
    .in6(register_bank_1_out_6), .in7(register_bank_1_out_7), .out(multiplexer_3_out), .sel(REG_3));
  _1_bit_register u_1_bit_register_1 (.DATA_IN(alu_1_zf), .CLK(CLK), .LOAD(ZFLD), .DATA_OUT(ZF));
  Control_Unit control_unit_1 (
    .OPCID(INSTRUCTION[14:12]), .ZF(ZF), .CLK(CLK), .IRLD(IRLD), .MEMLD(MEMLD), .MUX(MUX), .ZFLD(ZFLD),
    .REGLD(REGLD), .ARMUX(ARMUX), .PCINC(PCINC), .PCLD(PCLD));  // open: FETCH
  Program_Counter program_counter_1 (
    .PCINC(PCINC), .OFFSET(OFFSET), .PCLD(PCLD), .CLK(CLK), .MEM_ADDR(multiplexer_3_out[11:0]),
    .ARMUX(ARMUX), .ADDR(program_counter_1_addr));
  RAM #(.addrWidth(12), .dataWidth(16), .bus("separate")) ram_1 (
    .addr(program_counter_1_addr), .din(aaaa), .data(INSTRUCTION), .str(MEMLD), .clk(CLK));  // open: sel, ld, clr

  // Other names for the same wires on the sheet: INSTRUCTION_WO_OPCODE[11:0] = INSTRUCTION[11:0];
  //   OPCODE[2:0] = INSTRUCTION[14:12]
endmodule

module Register_Bank (
  input  REG_LOAD,
  input  [2:0] REG_SELECT,
  input  [15:0] IN,
  input  CLK,
  output [15:0] OUT_0,
  output [15:0] OUT_1,
  output [15:0] OUT_2,
  output [15:0] OUT_3,
  output [15:0] OUT_4,
  output [15:0] OUT_5,
  output [15:0] OUT_6,
  output [15:0] OUT_7
);

  wire decoder_1_out0, decoder_1_out1, decoder_1_out2, decoder_1_out3, decoder_1_out4, decoder_1_out5,
       decoder_1_out6, decoder_1_out7;

  Decoder #(.select(3), .disabled(0)) decoder_1 (
    .out0(decoder_1_out0), .out1(decoder_1_out1), .out2(decoder_1_out2), .out3(decoder_1_out3),
    .out4(decoder_1_out4), .out5(decoder_1_out5), .out6(decoder_1_out6), .out7(decoder_1_out7),
    .sel(REG_SELECT), .en(REG_LOAD));
  _16_bit_register u_16_bit_register_1 (.IN(IN), .LD(decoder_1_out0), .CLK(CLK), .OUT(OUT_0));
  _16_bit_register u_16_bit_register_2 (.IN(IN), .LD(decoder_1_out1), .CLK(CLK), .OUT(OUT_1));
  _16_bit_register u_16_bit_register_3 (.IN(IN), .LD(decoder_1_out2), .CLK(CLK), .OUT(OUT_2));
  _16_bit_register u_16_bit_register_4 (.IN(IN), .LD(decoder_1_out3), .CLK(CLK), .OUT(OUT_3));
  _16_bit_register u_16_bit_register_5 (.IN(IN), .LD(decoder_1_out4), .CLK(CLK), .OUT(OUT_4));
  _16_bit_register u_16_bit_register_6 (.IN(IN), .LD(decoder_1_out5), .CLK(CLK), .OUT(OUT_5));
  _16_bit_register u_16_bit_register_7 (.IN(IN), .LD(decoder_1_out6), .CLK(CLK), .OUT(OUT_6));
  _16_bit_register u_16_bit_register_8 (.IN(IN), .LD(decoder_1_out7), .CLK(CLK), .OUT(OUT_7));
endmodule

module ALU (
  input  [15:0] IN_0,
  input  [15:0] IN_1,
  input  [5:0] ALUOP,
  output [15:0] RESULT,
  output ZF
);

  wire [15:0] adder_1_out, adder_2_out, and_1_out, Bitwise_Or_out, Bitwise_Xor_out, multiplexer_1_out,
       not_1_out, subtractor_1_out, subtractor_2_out;

  Adder #(.width(16)) adder_1 (.a(IN_0), .b(IN_1), .out(adder_1_out));  // open: cin, cout
  Subtractor #(.width(16)) subtractor_1 (.a(IN_0), .b(IN_1), .out(subtractor_1_out));  // open: bin, bout
  assign and_1_out = IN_0 & IN_1;  // AND_Gate and_1, 16 bits wide
  assign Bitwise_Or_out = IN_0 | IN_1;  // OR_Gate Bitwise_Or, 16 bits wide
  assign Bitwise_Xor_out = IN_0 ^ IN_1;  // XOR_Gate Bitwise_Xor, 16 bits wide
  assign not_1_out = ~IN_1;  // NOT_Gate not_1, 16 bits wide
  Adder #(.width(16)) adder_2 (.a(IN_1), .b(16'h1), .out(adder_2_out));  // open: cin, cout
  Subtractor #(.width(16)) subtractor_2 (.a(IN_1), .b(16'h1), .out(subtractor_2_out));  // open: bin, bout
  Multiplexer #(.select(3), .width(16), .enable("false")) multiplexer_1 (
    .in0(not_1_out), .in1(IN_1), .in2(adder_2_out), .in3(subtractor_2_out), .out(multiplexer_1_out),
    .sel({1'b0, ALUOP[1:0]}));  // open: in4, in5, in6, in7
  Multiplexer #(.select(3), .width(16), .enable("false")) multiplexer_2 (
    .in0(adder_1_out), .in1(subtractor_1_out), .in2(and_1_out), .in3(Bitwise_Or_out), .in4(Bitwise_Xor_out),
    .in7(multiplexer_1_out), .out(RESULT), .sel(ALUOP[5:3]));  // open: in5, in6
  nor nor_1 (ZF, RESULT[0], RESULT[1], RESULT[2], RESULT[3], RESULT[4], RESULT[5], RESULT[6], RESULT[7], RESULT[8], RESULT[9], RESULT[10], RESULT[11], RESULT[12], RESULT[13], RESULT[14], RESULT[15]);
endmodule

module Control_Unit (
  input  [2:0] OPCID,
  input  ZF,
  input  CLK,
  output IRLD,
  output MEMLD,
  output MUX,
  output ZFLD,
  output REGLD,
  output ARMUX,
  output PCINC,
  output PCLD,
  output FETCH
);

  wire [1:1] and_1_out;
  wire [2:0] multiplexer_1_out, multiplexer_2_out, n3_bit_register_1_out;

  and and_1 (and_1_out[1], ~OPCID[0], ~OPCID[1], OPCID[2]);  // AND_Gate
  Multiplexer #(.select(2), .width(3), .disabled(0), .enable("false")) multiplexer_1 (
    .in0(OPCID), .in1(OPCID), .in2(3'b000), .in3(3'b101), .out(multiplexer_1_out), .sel({and_1_out[1], ZF}));
  Multiplexer #(.width(3), .enable("false")) multiplexer_2 (
    .in0(3'b000), .in1(multiplexer_1_out), .out(multiplexer_2_out), .sel(FETCH));
  _3_bit_register u_3_bit_register_1 (.IN(multiplexer_2_out), .CLK(CLK), .LD(1'b1), .OUT(n3_bit_register_1_out));
  ROM #(.addrWidth(3), .dataWidth(9)) rom_1 (
    .addr(n3_bit_register_1_out), .data({FETCH, PCLD, PCINC, ARMUX, REGLD, ZFLD, MUX, MEMLD, IRLD}));  // open: sel

  // Notes on the sheet:
  //   contents of rom_1 (hex, n*v repeats v):
  //   141 54 34 22 0 80 0 18
endmodule

module Program_Counter (
  input  PCINC,
  input  [11:0] OFFSET,
  input  PCLD,
  input  CLK,
  input  [11:0] MEM_ADDR,
  input  ARMUX,
  output [11:0] ADDR
);

  wire [11:0] adder_1_out, counter_1_out;

  Adder #(.width(12)) adder_1 (.a(counter_1_out), .b(OFFSET), .out(adder_1_out));  // open: cin, cout
  Counter counter_1 (.IN(adder_1_out), .PCINC(PCINC), .PCLD(PCLD), .CLK(CLK), .OUT(counter_1_out));
  Multiplexer #(.width(12), .enable("false")) multiplexer_1 (
    .in0(counter_1_out), .in1(MEM_ADDR), .out(ADDR), .sel(ARMUX));
endmodule

module _1_bit_register (
  input  DATA_IN,
  input  CLK,
  input  LOAD,
  output DATA_OUT
);

  wire not_1_out;

  not not_1 (not_1_out, DATA_IN);
  S_R_Flip_Flop s_r_ff_1 (.S(DATA_IN), .clk(CLK), .R(not_1_out), .Q(DATA_OUT), .en(LOAD));  // open: Qn, preset, reset
endmodule

module _12_bit_register (
  input  [11:0] IN,
  input  LD,
  input  CLK,
  output [11:0] OUT
);

  _3_bit_register u_3_bit_register_1 (.IN(IN[2:0]), .CLK(CLK), .LD(LD), .OUT(OUT[2:0]));
  _3_bit_register u_3_bit_register_2 (.IN(IN[5:3]), .CLK(CLK), .LD(LD), .OUT(OUT[5:3]));
  _3_bit_register u_3_bit_register_3 (.IN(IN[8:6]), .CLK(CLK), .LD(LD), .OUT(OUT[8:6]));
  _3_bit_register u_3_bit_register_4 (.IN(IN[11:9]), .CLK(CLK), .LD(LD), .OUT(OUT[11:9]));
endmodule

module _16_bit_register (
  input  [15:0] IN,
  input  LD,
  input  CLK,
  output [15:0] OUT
);

  _4_bit_register u_4_bit_register_1 (.IN(IN[3:0]), .LD(LD), .CLK(CLK), .OUT(OUT[3:0]));
  _4_bit_register u_4_bit_register_2 (.IN(IN[7:4]), .LD(LD), .CLK(CLK), .OUT(OUT[7:4]));
  _4_bit_register u_4_bit_register_3 (.IN(IN[11:8]), .LD(LD), .CLK(CLK), .OUT(OUT[11:8]));
  _4_bit_register u_4_bit_register_4 (.IN(IN[15:12]), .LD(LD), .CLK(CLK), .OUT(OUT[15:12]));
endmodule

module _3_bit_register (
  input  [2:0] IN,
  input  CLK,
  input  LD,
  output [2:0] OUT
);

  _1_bit_register u_1_bit_register_1 (.DATA_IN(IN[0]), .CLK(CLK), .LOAD(LD), .DATA_OUT(OUT[0]));
  _1_bit_register u_1_bit_register_2 (.DATA_IN(IN[1]), .CLK(CLK), .LOAD(LD), .DATA_OUT(OUT[1]));
  _1_bit_register u_1_bit_register_3 (.DATA_IN(IN[2]), .CLK(CLK), .LOAD(LD), .DATA_OUT(OUT[2]));
endmodule

module _4_bit_register (
  input  [3:0] IN,
  input  LD,
  input  CLK,
  output [3:0] OUT
);

  _1_bit_register u_1_bit_register_1 (.DATA_IN(IN[0]), .CLK(CLK), .LOAD(LD), .DATA_OUT(OUT[0]));
  _1_bit_register u_1_bit_register_2 (.DATA_IN(IN[1]), .CLK(CLK), .LOAD(LD), .DATA_OUT(OUT[1]));
  _1_bit_register u_1_bit_register_3 (.DATA_IN(IN[2]), .CLK(CLK), .LOAD(LD), .DATA_OUT(OUT[2]));
  _1_bit_register u_1_bit_register_4 (.DATA_IN(IN[3]), .CLK(CLK), .LOAD(LD), .DATA_OUT(OUT[3]));
endmodule

module Instructor_Register (
  input  [11:0] IN,
  input  CLK,
  input  LD,
  output [11:0] OUT,
  output [2:0] DST,
  output [2:0] SRC2,
  output [5:0] ALUOP,
  output [2:0] SRC1
);

  _12_bit_register u_12_bit_register_1 (.IN(IN), .LD(LD), .CLK(CLK), .OUT({ALUOP, OUT[5:3], DST}));

  assign {OUT[11:6], OUT[2:0]} = {ALUOP, DST};
  assign SRC1 = ALUOP[2:0];
  assign SRC2 = OUT[5:3];
endmodule

module Counter (
  input  [11:0] IN,
  input  PCINC,
  input  PCLD,
  input  CLK,
  output [11:0] OUT
);

  wire Bitwise_Or_out;
  wire [11:0] adder_1_out, multiplexer_1_out;

  Adder #(.width(12)) adder_1 (.a(OUT), .b(12'h1), .out(adder_1_out));  // open: cin, cout
  Multiplexer #(.width(12), .enable("false")) multiplexer_1 (
    .in0(IN), .in1(adder_1_out), .out(multiplexer_1_out), .sel(PCINC));
  or Bitwise_Or (Bitwise_Or_out, PCINC, PCLD);
  _12_bit_register u_12_bit_register_1 (.IN(multiplexer_1_out), .LD(Bitwise_Or_out), .CLK(CLK), .OUT(OUT));
endmodule
