// Logisim project 7_segment_driver.circ as structural Verilog: 2 circuits, main circuit main
module main (
  input  [3:0] in_1,
  output out_2,
  output out_3,
  output out_4,
  output out_5,
  output out_6,
  output out_7,
  output out_8
);

  wire [7:7] rom_1_data;

  ROM #(.addrWidth(4)) rom_1 (
    .addr(in_1), .data({rom_1_data[7], out_5, out_4, out_8, out_7, out_6, out_2, out_3}));  // open: sel
  _7_Segment_Display u_7_segment_display_1 (
    .g(out_5), .f(out_4), .a(out_3), .b(out_2), .e(out_8), .d(out_7), .c(out_6));  // open: dp

  // Notes on the sheet:
  //   contents of rom_1 (hex, n*v repeats v):
  //   3f 6 5b 4f 66 6d 7d 27 7f 6f 77 7c 39 5e 79 71
endmodule

module example_usages (
  input  [3:0] in_1,
  input  [3:0] in_2
);

  wire main_1_out_2, main_1_out_3, main_1_out_4, main_1_out_5, main_1_out_6, main_1_out_7, main_1_out_8,
       main_2_out_2, main_2_out_3, main_2_out_4, main_2_out_5, main_3_out_6, main_3_out_7, main_3_out_8;

  main main_1 (
    .in_1(in_1), .out_2(main_1_out_2), .out_3(main_1_out_3), .out_4(main_1_out_4), .out_5(main_1_out_5),
    .out_6(main_1_out_6), .out_7(main_1_out_7), .out_8(main_1_out_8));
  _7_Segment_Display u_7_segment_display_1 (
    .g(main_1_out_5), .f(main_1_out_4), .a(main_1_out_3), .b(main_1_out_2), .e(main_1_out_8),
    .d(main_1_out_7), .c(main_1_out_6));  // open: dp
  main main_2 (
    .in_1(in_2), .out_2(main_2_out_2), .out_3(main_2_out_3), .out_4(main_2_out_4), .out_5(main_2_out_5));  // open: out_6, out_7, out_8
  _7_Segment_Display u_7_segment_display_2 (
    .g(main_2_out_5), .f(main_2_out_4), .a(main_2_out_3), .b(main_2_out_2), .e(main_3_out_8),
    .d(main_3_out_7), .c(main_3_out_6));  // open: dp
  main main_3 (
    .in_1(in_2), .out_6(main_3_out_6), .out_7(main_3_out_7), .out_8(main_3_out_8));  // open: out_2, out_3, out_4, out_5
endmodule
