// Logisim project reptile_8.circ as structural Verilog
module main (
);

  wire [3:0] undriven;
  wire [3:1] undriven_2, undriven_3, undriven_4, undriven_5;

  register_bank register_bank_1 ();
  Hex_Digit_Display hex_digit_display_1 (.value({undriven_2, undriven[0]}));  // open: dp
  Hex_Digit_Display hex_digit_display_2 (.value({undriven_3, undriven[1]}));  // open: dp
  Hex_Digit_Display hex_digit_display_3 (.value({undriven_4, undriven[3]}));  // open: dp
  Hex_Digit_Display hex_digit_display_4 (.value({undriven_5, undriven[2]}));  // open: dp
  // Pins of 1 and 4 bits meet at {undriven_4, undriven[3]}
  // Pins of 1 and 4 bits meet at {undriven_3, undriven[1]}
  // Pins of 1 and 4 bits meet at {undriven_2, undriven[0]}
  // Pins of 1 and 4 bits meet at {undriven_5, undriven[2]}
endmodule
