// Logisim project frog.circ as structural Verilog: 13 circuits, main circuit main
module main (
  output [15:0] out_1,
  output [15:0] out_2,
  output [15:0] out_3,
  output [15:0] out_4
);

  wire CLK, IRLD, LD, MUX, PCINC;
  wire [1:0] REG_1, REG_2, REG_3;
  wire [3:0] ALUOP;
  wire [11:0] ADDR_OUT;
  wire [15:0] ALU_RESULT, INSTRUCTION, multiplexer_1_out, multiplexer_2_out, multiplexer_3_out, OUT_0;

  Clock clock_1 (.out(CLK));
  Multiplexer #(.width(16), .enable("false")) multiplexer_1 (
    .in0(ALU_RESULT), .in1(INSTRUCTION), .out(multiplexer_1_out), .sel(MUX));
  Register_Bank register_bank_1 (
    .REG_SELECT(REG_1), .CLK(CLK), .REG_LOAD(LD), .IN(multiplexer_1_out), .OUT_1(out_2), .OUT_0(OUT_0),
    .OUT_2(out_3), .OUT_3(out_4));
  Instructor_Register instructor_register_1 (
    .IN(INSTRUCTION[11:0]), .CLK(CLK), .LD(IRLD), .DST(REG_1), .SRC2(REG_3), .SRC1(REG_2), .ALUOP(ALUOP));
  Multiplexer #(.select(2), .width(16), .enable("false")) multiplexer_2 (
    .in0(OUT_0), .in1(out_2), .in2(out_3), .in3(out_4), .out(multiplexer_2_out), .sel(REG_2));
  ALU alu_1 (.IN_0(multiplexer_2_out), .IN_1(multiplexer_3_out), .RESULT(ALU_RESULT), .ALUOP(ALUOP));
  Multiplexer #(.select(2), .width(16), .enable("false")) multiplexer_3 (
    .in0(OUT_0), .in1(out_2), .in2(out_3), .in3(out_4), .out(multiplexer_3_out), .sel(REG_3));
  Program_Counter program_counter_1 (.PCINC(PCINC), .CLK(CLK), .ADDR(ADDR_OUT));
  Control_Unit control_unit_1 (
    .CLK(CLK), .IRLD(IRLD), .MUX(MUX), .PCINC(PCINC), .LD(LD), .OPCODE(INSTRUCTION[13:12]));  // open: FETCH
  RAM #(.addrWidth(12), .dataWidth(16), .bus("separate")) ram_1 (
    .addr(ADDR_OUT), .data(INSTRUCTION), .clk(CLK));  // open: din, str, sel, ld, clr

  // Other names for the same wires on the sheet: INSTRUCTION_BODY[11:0] = INSTRUCTION[11:0];
  //   OPCODE[1:0] = INSTRUCTION[13:12]; OUT_1_t[15:0] = out_2; OUT_2_t[15:0] = out_3; OUT_3_t[15:0] = out_4;
  //   REG_0[15:0] = out_1
endmodule

module Register_Bank (
  input  REG_LOAD,
  input  [1:0] REG_SELECT,
  input  [15:0] IN,
  input  CLK,
  output [15:0] OUT_0,
  output [15:0] OUT_1,
  output [15:0] OUT_2,
  output [15:0] OUT_3
);

  wire decoder_1_out0, decoder_1_out1, decoder_1_out2, decoder_1_out3;

  Decoder #(.select(2), .disabled(0)) decoder_1 (
    .out0(decoder_1_out0), .out1(decoder_1_out1), .out2(decoder_1_out2), .out3(decoder_1_out3),
    .sel(REG_SELECT), .en(REG_LOAD));
  _16_bit_register u_16_bit_register_1 (.IN(IN), .LD(decoder_1_out0), .CLK(CLK), .OUT(OUT_0));
  _16_bit_register u_16_bit_register_2 (.IN(IN), .LD(decoder_1_out1), .CLK(CLK), .OUT(OUT_1));
  _16_bit_register u_16_bit_register_3 (.IN(IN), .LD(decoder_1_out2), .CLK(CLK), .OUT(OUT_2));
  _16_bit_register u_16_bit_register_4 (.IN(IN), .LD(decoder_1_out3), .CLK(CLK), .OUT(OUT_3));
endmodule

module ALU (
  input  [15:0] IN_0,
  input  [15:0] IN_1,
  input  [3:0] ALUOP,
  output [15:0] RESULT
);

  wire [15:0] adder_1_out, adder_2_out, and_1_out, Bitwise_Or_out, Bitwise_Xor_out, not_1_out,
       subtractor_1_out, subtractor_2_out;

  Adder #(.width(16)) adder_1 (.a(IN_0), .b(IN_1), .out(adder_1_out));  // open: cin, cout
  Subtractor #(.width(16)) subtractor_1 (.a(IN_0), .b(IN_1), .out(subtractor_1_out));  // open: bin, bout
  assign and_1_out = IN_0 & IN_1;  // AND_Gate and_1, 16 bits wide
  assign Bitwise_Or_out = IN_0 | IN_1;  // OR_Gate Bitwise_Or, 16 bits wide
  assign Bitwise_Xor_out = IN_0 ^ IN_1;  // XOR_Gate Bitwise_Xor, 16 bits wide
  assign not_1_out = ~IN_1;  // NOT_Gate not_1, 16 bits wide
  Adder #(.width(16)) adder_2 (.a(IN_1), .b(16'h1), .out(adder_2_out));  // open: cin, cout
  Subtractor #(.width(16)) subtractor_2 (.a(IN_1), .b(16'h1), .out(subtractor_2_out));  // open: bin, bout
  Multiplexer #(.select(4), .width(16), .enable("false")) multiplexer_1 (
    .in0(adder_1_out), .in1(subtractor_1_out), .in2(and_1_out), .in3(Bitwise_Or_out), .in4(Bitwise_Xor_out),
    .in5(not_1_out), .in6(IN_1), .in7(adder_2_out), .in8(subtractor_2_out), .out(RESULT), .sel(ALUOP));  // open: in9, in10, in11, in12, in13, in14, in15
endmodule

module Control_Unit (
  input  [1:0] OPCODE,
  input  CLK,
  output PCINC,
  output LD,
  output IRLD,
  output MUX,
  output FETCH
);

  wire [1:0] multiplexer_1_out, n2_bit_register_1_out;

  Multiplexer #(.width(2), .enable("false")) multiplexer_1 (
    .in0(2'b00), .in1(OPCODE), .out(multiplexer_1_out), .sel(FETCH));
  _2_bit_register u_2_bit_register_1 (.IN(multiplexer_1_out), .CLK(CLK), .LD(1'b1), .OUT(n2_bit_register_1_out));
  ROM #(.addrWidth(2), .dataWidth(5)) rom_1 (
    .addr(n2_bit_register_1_out), .data({FETCH, MUX, IRLD, LD, PCINC}));  // open: sel

  // Notes on the sheet:
  //   contents of rom_1 (hex, n*v repeats v):
  //   18 2 7
endmodule

module Program_Counter (
  input  PCINC,
  input  CLK,
  output [11:0] ADDR
);

  Counter counter_1 (.PCINC(PCINC), .PCLD(1'b0), .CLK(CLK), .OUT(ADDR));  // open: IN
endmodule

module _1_bit_register (
  input  DATA_IN,
  input  CLK,
  input  LOAD,
  output DATA_OUT
);

  wire not_1_out;

  not not_1 (not_1_out, DATA_IN);
  S_R_Flip_Flop s_r_ff_1 (.S(DATA_IN), .clk(CLK), .R(not_1_out), .Q(DATA_OUT), .en(LOAD));  // open: Qn, preset, reset
endmodule

module _12_bit_register (
  input  [11:0] IN,
  input  LD,
  input  CLK,
  output [11:0] OUT
);

  _3_bit_register u_3_bit_register_1 (.IN(IN[2:0]), .CLK(CLK), .LD(LD), .OUT(OUT[2:0]));
  _3_bit_register u_3_bit_register_2 (.IN(IN[5:3]), .CLK(CLK), .LD(LD), .OUT(OUT[5:3]));
  _3_bit_register u_3_bit_register_3 (.IN(IN[8:6]), .CLK(CLK), .LD(LD), .OUT(OUT[8:6]));
  _3_bit_register u_3_bit_register_4 (.IN(IN[11:9]), .CLK(CLK), .LD(LD), .OUT(OUT[11:9]));
endmodule

module _16_bit_register (
  input  [15:0] IN,
  input  LD,
  input  CLK,
  output [15:0] OUT
);

  _4_bit_register u_4_bit_register_1 (.IN(IN[3:0]), .LD(LD), .CLK(CLK), .OUT(OUT[3:0]));
  _4_bit_register u_4_bit_register_2 (.IN(IN[7:4]), .LD(LD), .CLK(CLK), .OUT(OUT[7:4]));
  _4_bit_register u_4_bit_register_3 (.IN(IN[11:8]), .LD(LD), .CLK(CLK), .OUT(OUT[11:8]));
  _4_bit_register u_4_bit_register_4 (.IN(IN[15:12]), .LD(LD), .CLK(CLK), .OUT(OUT[15:12]));
endmodule

module _3_bit_register (
  input  [2:0] IN,
  input  CLK,
  input  LD,
  output [2:0] OUT
);

  _1_bit_register u_1_bit_register_1 (.DATA_IN(IN[0]), .CLK(CLK), .LOAD(LD), .DATA_OUT(OUT[0]));
  _1_bit_register u_1_bit_register_2 (.DATA_IN(IN[1]), .CLK(CLK), .LOAD(LD), .DATA_OUT(OUT[1]));
  _1_bit_register u_1_bit_register_3 (.DATA_IN(IN[2]), .CLK(CLK), .LOAD(LD), .DATA_OUT(OUT[2]));
endmodule

module _4_bit_register (
  input  [3:0] IN,
  input  LD,
  input  CLK,
  output [3:0] OUT
);

  _1_bit_register u_1_bit_register_1 (.DATA_IN(IN[0]), .CLK(CLK), .LOAD(LD), .DATA_OUT(OUT[0]));
  _1_bit_register u_1_bit_register_2 (.DATA_IN(IN[1]), .CLK(CLK), .LOAD(LD), .DATA_OUT(OUT[1]));
  _1_bit_register u_1_bit_register_3 (.DATA_IN(IN[2]), .CLK(CLK), .LOAD(LD), .DATA_OUT(OUT[2]));
  _1_bit_register u_1_bit_register_4 (.DATA_IN(IN[3]), .CLK(CLK), .LOAD(LD), .DATA_OUT(OUT[3]));
endmodule

module Instructor_Register (
  input  [11:0] IN,
  input  CLK,
  input  LD,
  output [1:0] DST,
  output [1:0] SRC2,
  output [1:0] SRC1,
  output [3:0] ALUOP
);

  wire [5:2] n12_bit_register_1_out;

  _12_bit_register u_12_bit_register_1 (
    .IN(IN), .LD(LD), .CLK(CLK),
    .OUT({ALUOP, SRC1, n12_bit_register_1_out[5], SRC2, n12_bit_register_1_out[2], DST}));
endmodule

module Counter (
  input  [11:0] IN,
  input  PCINC,
  input  PCLD,
  input  CLK,
  output [11:0] OUT
);

  wire Bitwise_Or_out;
  wire [11:0] adder_1_out, multiplexer_1_out;

  Adder #(.width(12)) adder_1 (.a(OUT), .b(12'h1), .out(adder_1_out));  // open: cin, cout
  Multiplexer #(.width(12), .enable("false")) multiplexer_1 (
    .in0(IN), .in1(adder_1_out), .out(multiplexer_1_out), .sel(PCINC));
  or Bitwise_Or (Bitwise_Or_out, PCINC, PCLD);
  _12_bit_register u_12_bit_register_1 (.IN(multiplexer_1_out), .LD(Bitwise_Or_out), .CLK(CLK), .OUT(OUT));
endmodule

module _2_bit_register (
  input  [1:0] IN,
  input  CLK,
  input  LD,
  output [1:0] OUT
);

  _1_bit_register u_1_bit_register_1 (.DATA_IN(IN[0]), .CLK(CLK), .LOAD(LD), .DATA_OUT(OUT[0]));
  _1_bit_register u_1_bit_register_2 (.DATA_IN(IN[1]), .CLK(CLK), .LOAD(LD), .DATA_OUT(OUT[1]));
endmodule
