// Logisim project bird.circ as structural Verilog
module Register_Bank (
  input  REG_LOAD,
  input  [2:0] REG_SELECT,
  input  [15:0] IN,
  input  SP_plus_plus,
  input  SP_minus_minus,
  input  CLK,
  output [15:0] OUT_0,
  output [15:0] OUT_1,
  output [15:0] OUT_2,
  output [15:0] OUT_3,
  output [15:0] OUT_4,
  output [15:0] OUT_5,
  output [15:0] OUT_6,
  output [15:0] OUT_7
);

  wire decoder_1_out0, decoder_1_out1, decoder_1_out2, decoder_1_out3, decoder_1_out4, decoder_1_out5,
       decoder_1_out6;

  Decoder #(.select(3), .disabled(0)) decoder_1 (
    .out0(decoder_1_out0), .out1(decoder_1_out1), .out2(decoder_1_out2), .out3(decoder_1_out3),
    .out4(decoder_1_out4), .out5(decoder_1_out5), .out6(decoder_1_out6), .sel(REG_SELECT), .en(REG_LOAD));  // open: out7
  _16_bit_register u_16_bit_register_1 (.IN(IN), .LD(decoder_1_out0), .CLK(CLK), .OUT(OUT_0));
  _16_bit_register u_16_bit_register_2 (.IN(IN), .LD(decoder_1_out1), .CLK(CLK), .OUT(OUT_1));
  _16_bit_register u_16_bit_register_3 (.IN(IN), .LD(decoder_1_out2), .CLK(CLK), .OUT(OUT_2));
  _16_bit_register u_16_bit_register_4 (.IN(IN), .LD(decoder_1_out3), .CLK(CLK), .OUT(OUT_3));
  _16_bit_register u_16_bit_register_5 (.IN(IN), .LD(decoder_1_out4), .CLK(CLK), .OUT(OUT_4));
  _16_bit_register u_16_bit_register_6 (.IN(IN), .LD(decoder_1_out5), .CLK(CLK), .OUT(OUT_5));
  _16_bit_register u_16_bit_register_7 (.IN(IN), .LD(decoder_1_out6), .CLK(CLK), .OUT(OUT_6));
  stack_register stack_register_1 (
    .SP_plus_plus(SP_plus_plus), .SP_minus_minus(SP_minus_minus), .out_4(OUT_7), .CLK(CLK));
endmodule

module ALU (
  input  [15:0] IN_0,
  input  [15:0] IN_1,
  input  [5:0] ALUOP,
  output [15:0] RESULT,
  output ZF
);

  wire [15:0] adder_1_out, adder_2_out, and_1_out, Bitwise_Or_out, Bitwise_Xor_out, multiplexer_1_out,
       not_1_out, subtractor_1_out, subtractor_2_out;

  Adder #(.width(16)) adder_1 (.a(IN_0), .b(IN_1), .out(adder_1_out));  // open: cin, cout
  Subtractor #(.width(16)) subtractor_1 (.a(IN_0), .b(IN_1), .out(subtractor_1_out));  // open: bin, bout
  assign and_1_out = IN_0 & IN_1;  // AND_Gate and_1, 16 bits wide
  assign Bitwise_Or_out = IN_0 | IN_1;  // OR_Gate Bitwise_Or, 16 bits wide
  assign Bitwise_Xor_out = IN_0 ^ IN_1;  // XOR_Gate Bitwise_Xor, 16 bits wide
  assign not_1_out = ~IN_1;  // NOT_Gate not_1, 16 bits wide
  Adder #(.width(16)) adder_2 (.a(IN_1), .b(16'h1), .out(adder_2_out));  // open: cin, cout
  Subtractor #(.width(16)) subtractor_2 (.a(IN_1), .b(16'h1), .out(subtractor_2_out));  // open: bin, bout
  Multiplexer #(.select(3), .width(16), .enable("false")) multiplexer_1 (
    .in0(not_1_out), .in1(IN_1), .in2(adder_2_out), .in3(subtractor_2_out), .out(multiplexer_1_out),
    .sel({1'b0, ALUOP[1:0]}));  // open: in4, in5, in6, in7
  Multiplexer #(.select(3), .width(16), .enable("false")) multiplexer_2 (
    .in0(adder_1_out), .in1(subtractor_1_out), .in2(and_1_out), .in3(Bitwise_Or_out), .in4(Bitwise_Xor_out),
    .in7(multiplexer_1_out), .out(RESULT), .sel(ALUOP[5:3]));  // open: in5, in6
  nor nor_1 (ZF, RESULT[0], RESULT[1], RESULT[2], RESULT[3], RESULT[4], RESULT[5], RESULT[6], RESULT[7], RESULT[8], RESULT[9], RESULT[10], RESULT[11], RESULT[12], RESULT[13], RESULT[14], RESULT[15]);
endmodule

// ARMUX
module Control_Unit (
  input  [3:0] OPCID,
  input  ZF,
  input  CLK,
  output CLI,
  output INTLD,
  output STI,
  output FLAGLD,
  output IRLD,
  output MEMLD,
  output MUX,
  output ZFLD,
  output REGLD,
  output [1:0] ARMUX,
  output PCINC,
  output PCLD,
  output SP_minus_minus,
  output SP_plus_plus,
  output PCMUX,
  output [1:0] DATAMUX,
  output FETCH
);

  wire FETCH_t;
  wire [1:1] and_1_out;
  wire [3:0] multiplexer_1_out, NEXT_ADDR;
  wire [4:0] multiplexer_3_out, n5_bit_register_1_out;
  wire [16:16] rom_1_data;

  and and_1 (and_1_out[1], ~OPCID[1], OPCID[3]);  // AND_Gate
  Multiplexer #(.select(2), .width(4), .disabled(0), .enable("false")) multiplexer_1 (
    .in0(OPCID), .in1(OPCID), .in2(4'b0000), .in3(4'b1101), .out(multiplexer_1_out), .sel({and_1_out[1], ZF}));
  Multiplexer #(.width(4), .enable("false")) multiplexer_2 (
    .in0(NEXT_ADDR), .in1(multiplexer_1_out), .sel(FETCH_t));  // open: out
  Multiplexer #(.width(5), .enable("false")) multiplexer_3 (.out(multiplexer_3_out));  // open: in0, in1, sel
  _5_bit_register u_5_bit_register_1 (.IN(multiplexer_3_out), .LD(1'b1), .CLK(CLK), .OUT(n5_bit_register_1_out));
  ROM #(.addrWidth(5), .dataWidth(18)) rom_1 (
    .addr(n5_bit_register_1_out),
    .data({FETCH_t, rom_1_data[16], PCMUX, SP_plus_plus, SP_minus_minus, PCLD, PCINC, ARMUX, REGLD, ZFLD, MUX, MEMLD, IRLD, NEXT_ADDR}));  // open: sel

  // Notes on the sheet:
  //   contents of rom_1 (hex, n*v repeats v):
  //   810 940 340 220 0 180 2420 400c 15420 400d 540 9440
endmodule

module Program_Counter (
  input  PCMUX,
  input  [11:0] OFFSET,
  input  [15:0] INSTRUCTION,
  input  PCINC,
  input  PCLD,
  input  CLK,
  input  [1:0] ARMUX,
  input  [15:0] MEM_ADDR,
  input  [15:0] STACK_POINTER,
  output [11:0] PC_VAL,
  output [11:0] ADDR
);

  wire [11:0] adder_1_out, multiplexer_1_out;

  Adder #(.width(12)) adder_1 (.a(PC_VAL), .b(OFFSET), .out(adder_1_out));  // open: cin, cout
  Multiplexer #(.width(12), .enable("false")) multiplexer_1 (
    .in0(adder_1_out), .in1(INSTRUCTION[11:0]), .out(multiplexer_1_out), .sel(PCMUX));
  Counter counter_1 (.IN(multiplexer_1_out), .PCINC(PCINC), .PCLD(PCLD), .CLK(CLK), .OUT(PC_VAL));
  Multiplexer #(.select(2), .width(12), .enable("false")) multiplexer_2 (
    .in0(PC_VAL), .in1(MEM_ADDR[11:0]), .in2(STACK_POINTER[11:0]), .out(ADDR), .sel(ARMUX));  // open: in3
endmodule

module _1_bit_register (
  input  DATA_IN,
  input  CLK,
  input  LOAD,
  output DATA_OUT
);

  wire not_1_out;

  not not_1 (not_1_out, DATA_IN);
  S_R_Flip_Flop s_r_ff_1 (.S(DATA_IN), .clk(CLK), .R(not_1_out), .Q(DATA_OUT), .en(LOAD));  // open: Qn, preset, reset
endmodule

module _12_bit_register (
  input  [11:0] IN,
  input  LD,
  input  CLK,
  output [11:0] OUT
);

  _3_bit_register u_3_bit_register_1 (.IN(IN[2:0]), .CLK(CLK), .LD(LD), .OUT(OUT[2:0]));
  _3_bit_register u_3_bit_register_2 (.IN(IN[5:3]), .CLK(CLK), .LD(LD), .OUT(OUT[5:3]));
  _3_bit_register u_3_bit_register_3 (.IN(IN[8:6]), .CLK(CLK), .LD(LD), .OUT(OUT[8:6]));
  _3_bit_register u_3_bit_register_4 (.IN(IN[11:9]), .CLK(CLK), .LD(LD), .OUT(OUT[11:9]));
endmodule

module _16_bit_register (
  input  [15:0] IN,
  input  LD,
  input  CLK,
  output [15:0] OUT
);

  _4_bit_register u_4_bit_register_1 (.IN(IN[3:0]), .LD(LD), .CLK(CLK), .OUT(OUT[3:0]));
  _4_bit_register u_4_bit_register_2 (.IN(IN[7:4]), .LD(LD), .CLK(CLK), .OUT(OUT[7:4]));
  _4_bit_register u_4_bit_register_3 (.IN(IN[11:8]), .LD(LD), .CLK(CLK), .OUT(OUT[11:8]));
  _4_bit_register u_4_bit_register_4 (.IN(IN[15:12]), .LD(LD), .CLK(CLK), .OUT(OUT[15:12]));
endmodule

module _3_bit_register (
  input  [2:0] IN,
  input  CLK,
  input  LD,
  output [2:0] OUT
);

  _1_bit_register u_1_bit_register_1 (.DATA_IN(IN[0]), .CLK(CLK), .LOAD(LD), .DATA_OUT(OUT[0]));
  _1_bit_register u_1_bit_register_2 (.DATA_IN(IN[1]), .CLK(CLK), .LOAD(LD), .DATA_OUT(OUT[1]));
  _1_bit_register u_1_bit_register_3 (.DATA_IN(IN[2]), .CLK(CLK), .LOAD(LD), .DATA_OUT(OUT[2]));
endmodule

module _4_bit_register (
  input  [3:0] IN,
  input  LD,
  input  CLK,
  output [3:0] OUT
);

  _1_bit_register u_1_bit_register_1 (.DATA_IN(IN[0]), .CLK(CLK), .LOAD(LD), .DATA_OUT(OUT[0]));
  _1_bit_register u_1_bit_register_2 (.DATA_IN(IN[1]), .CLK(CLK), .LOAD(LD), .DATA_OUT(OUT[1]));
  _1_bit_register u_1_bit_register_3 (.DATA_IN(IN[2]), .CLK(CLK), .LOAD(LD), .DATA_OUT(OUT[2]));
  _1_bit_register u_1_bit_register_4 (.DATA_IN(IN[3]), .CLK(CLK), .LOAD(LD), .DATA_OUT(OUT[3]));
endmodule

module Instructor_Register (
  input  [11:0] IN,
  input  CLK,
  input  LD,
  output [11:0] OUT,
  output [2:0] DST,
  output [2:0] SRC2,
  output [5:0] ALUOP,
  output [2:0] SRC1
);

  _12_bit_register u_12_bit_register_1 (.IN(IN), .LD(LD), .CLK(CLK), .OUT({ALUOP, OUT[5:3], DST}));

  assign {OUT[11:6], OUT[2:0]} = {ALUOP, DST};
  assign SRC1 = ALUOP[2:0];
  assign SRC2 = OUT[5:3];
endmodule

module Counter (
  input  [11:0] IN,
  input  PCINC,
  input  PCLD,
  input  CLK,
  output [11:0] OUT
);

  wire Bitwise_Or_out;
  wire [11:0] adder_1_out, multiplexer_1_out;

  Adder #(.width(12)) adder_1 (.a(OUT), .b(12'h1), .out(adder_1_out));  // open: cin, cout
  Multiplexer #(.width(12), .enable("false")) multiplexer_1 (
    .in0(IN), .in1(adder_1_out), .out(multiplexer_1_out), .sel(PCINC));
  or Bitwise_Or (Bitwise_Or_out, PCINC, PCLD);
  _12_bit_register u_12_bit_register_1 (.IN(multiplexer_1_out), .LD(Bitwise_Or_out), .CLK(CLK), .OUT(OUT));
endmodule

module Bird_CPU (
  input  [15:0] DATA_IN,
  input  CLK,
  output MEMLD,
  output [11:0] ADDR_OUT,
  output [15:0] DATA_OUT
);

  wire alu_1_zf, IRLD, MUX, PCINC, PCLD, PCMUX, REGLD, SP_minus_minus, SP_plus_plus, ZF, ZFLD;
  wire [1:0] ARMUX, DATAMUX;
  wire [2:0] REG_1, REG_2, REG_3;
  wire [5:0] ALUOP;
  wire [11:0] OFFSET, PCVAL;
  wire [15:0] aaaa, ALU_RESULT, ALURES, multiplexer_1_out, register_bank_1_out_0, register_bank_1_out_1,
       register_bank_1_out_2, register_bank_1_out_3, register_bank_1_out_4, register_bank_1_out_5,
       register_bank_1_out_6, STACK_POINTER;
  wire [15:12] undriven;

  Multiplexer #(.width(16), .enable("false")) multiplexer_1 (
    .in0(ALU_RESULT), .in1(DATA_IN), .out(multiplexer_1_out), .sel(MUX));
  Register_Bank register_bank_1 (
    .REG_SELECT(REG_1), .CLK(CLK), .OUT_1(register_bank_1_out_1), .OUT_0(register_bank_1_out_0),
    .OUT_2(register_bank_1_out_2), .OUT_3(register_bank_1_out_3), .OUT_4(register_bank_1_out_4),
    .OUT_5(register_bank_1_out_5), .OUT_6(register_bank_1_out_6), .OUT_7(STACK_POINTER), .REG_LOAD(REGLD),
    .IN(multiplexer_1_out), .SP_plus_plus(SP_minus_minus), .SP_minus_minus(SP_plus_plus));
  Multiplexer #(.select(3), .width(16), .enable("false")) multiplexer_2 (
    .in0(register_bank_1_out_0), .in1(register_bank_1_out_1), .in2(register_bank_1_out_2),
    .in3(register_bank_1_out_3), .in4(register_bank_1_out_4), .in5(register_bank_1_out_5),
    .in6(register_bank_1_out_6), .in7(STACK_POINTER), .out(aaaa), .sel(REG_2));
  Instructor_Register instructor_register_1 (
    .IN(DATA_IN[11:0]), .CLK(CLK), .LD(IRLD), .OUT(OFFSET), .DST(REG_1), .SRC2(REG_3), .SRC1(REG_2),
    .ALUOP(ALUOP));
  ALU alu_1 (.IN_0(aaaa), .IN_1(ALURES), .RESULT(ALU_RESULT), .ZF(alu_1_zf), .ALUOP(ALUOP));
  Multiplexer #(.select(3), .width(16), .enable("false")) multiplexer_3 (
    .in0(register_bank_1_out_0), .in1(register_bank_1_out_1), .in2(register_bank_1_out_2),
    .in3(register_bank_1_out_3), .in4(register_bank_1_out_4), .in5(register_bank_1_out_5),
    .in6(register_bank_1_out_6), .in7(STACK_POINTER), .out(ALURES), .sel(REG_3));
  _1_bit_register u_1_bit_register_1 (.DATA_IN(alu_1_zf), .CLK(CLK), .LOAD(ZFLD), .DATA_OUT(ZF));
  Control_Unit control_unit_1 (
    .OPCID(DATA_IN[15:12]), .ZF(ZF), .CLK(CLK), .IRLD(IRLD), .MEMLD(MEMLD), .MUX(MUX), .ZFLD(ZFLD),
    .REGLD(REGLD), .PCINC(PCINC), .PCLD(PCLD), .DATAMUX(DATAMUX), .ARMUX(ARMUX), .SP_plus_plus(SP_plus_plus),
    .SP_minus_minus(SP_minus_minus), .PCMUX(PCMUX));  // open: FETCH, INTLD, FLAGLD, CLI, STI
  Multiplexer #(.width(16), .enable("false")) multiplexer_4 (
    .in0(aaaa), .in1({undriven, PCVAL}), .out(DATA_OUT), .sel(DATAMUX[0]));
  Program_Counter program_counter_1 (
    .PCINC(PCINC), .OFFSET(OFFSET), .PCLD(PCLD), .CLK(CLK), .MEM_ADDR(ALURES), .ARMUX(ARMUX),
    .ADDR(ADDR_OUT), .STACK_POINTER(STACK_POINTER), .PCMUX(PCMUX), .INSTRUCTION(DATA_IN), .PC_VAL(PCVAL));
  // Pins of 1 and 2 bits meet at DATAMUX

  // Other names for the same wires on the sheet: INSTRUCTION[15:0] = DATA_IN; INSTRUCTION_BODY[11:0] = DATA_IN[11:0];
  //   OPCODE[3:0] = DATA_IN[15:12]; PCOUT[11:0] = ADDR_OUT
endmodule

module stack_register (
  input  SP_plus_plus,
  input  SP_minus_minus,
  input  CLK,
  output [15:0] out_4
);

  wire Bitwise_Or_out;
  wire [15:0] adder_1_out, multiplexer_1_out, subtractor_1_out;

  Adder #(.width(16)) adder_1 (.a(out_4), .b(16'h1), .out(adder_1_out));  // open: cin, cout
  Subtractor #(.width(16)) subtractor_1 (.a(out_4), .b(16'h1), .out(subtractor_1_out));  // open: bin, bout
  or Bitwise_Or (Bitwise_Or_out, SP_plus_plus, SP_minus_minus);
  Multiplexer #(.select(2), .width(16), .enable("false")) multiplexer_1 (
    .in1(adder_1_out), .in2(subtractor_1_out), .out(multiplexer_1_out), .sel({SP_minus_minus, SP_plus_plus}));  // open: in0, in3
  _16_bit_register u_16_bit_register_1 (.IN(multiplexer_1_out), .LD(Bitwise_Or_out), .CLK(CLK), .OUT(out_4));
endmodule

module _5_bit_register (
  input  [4:0] IN,
  input  LD,
  input  CLK,
  output [4:0] OUT
);

  _1_bit_register u_1_bit_register_1 (.DATA_IN(IN[0]), .CLK(CLK), .LOAD(LD), .DATA_OUT(OUT[0]));
  _1_bit_register u_1_bit_register_2 (.DATA_IN(IN[1]), .CLK(CLK), .LOAD(LD), .DATA_OUT(OUT[1]));
  _1_bit_register u_1_bit_register_3 (.DATA_IN(IN[2]), .CLK(CLK), .LOAD(LD), .DATA_OUT(OUT[2]));
  _1_bit_register u_1_bit_register_4 (.DATA_IN(IN[3]), .CLK(CLK), .LOAD(LD), .DATA_OUT(OUT[3]));
  _1_bit_register u_1_bit_register_5 (.DATA_IN(IN[4]), .CLK(CLK), .LOAD(LD), .DATA_OUT(OUT[4]));
endmodule
