// Logisim project 7_segment_driver.circ as structural Verilog: 1 circuit, main circuit main
module main (
  input  [3:0] in_1,
  output out_2,
  output out_3,
  output out_4,
  output out_5,
  output out_6,
  output out_7,
  output out_8
);

  wire [7:7] rom_1_data;

  ROM #(.addrWidth(4)) rom_1 (
    .addr(in_1), .data({rom_1_data[7], out_5, out_4, out_8, out_7, out_6, out_2, out_3}));  // open: sel
  _7_Segment_Display u_7_segment_display_1 (
    .g(out_5), .f(out_4), .a(out_3), .b(out_2), .e(out_8), .d(out_7), .c(out_6));  // open: dp

  // Notes on the sheet:
  //   contents of rom_1 (hex, n*v repeats v):
  //   3f 6 5b 4f 66 6d 7d 27 7f 6f 77 7c 39 5e 79 71
endmodule
