// Logisim project project_2.circ as structural Verilog: 2 circuits, main circuit main
module main (
  input  [15:0] Pin_1,
  input  [15:0] Pin_2
);

  wire _7_SEG_LD, ADDR_0, and_1_out, CLK, CS, main_1_out_6, main_1_out_7, main_1_out_8, main_2_out_2,
       main_2_out_3, main_2_out_4, main_2_out_5, main_3_out_2, main_3_out_3, main_3_out_4, main_3_out_5,
       main_4_out_6, main_4_out_7, main_4_out_8, main_5_out_2, main_5_out_3, main_5_out_4, main_5_out_5,
       main_6_out_6, main_6_out_7, main_6_out_8, main_7_out_2, main_7_out_3, main_7_out_4, main_7_out_5,
       main_8_out_6, main_8_out_7, main_8_out_8, MEMLD, not_1_out, not_2_out, not_3_out, not_4_out,
       not_5_out, not_6_out, not_7_out, not_8_out, PB_1, PB_2, undriven, undriven_2, undriven_3;
  wire [3:0] DISP_0, DISP_1, DISP_2, DISP_3;
  wire [15:0] DATA_IN, DATA_OUT, input_thing_1_out, multiplexer_1_out;
  wire [15:2] ADDR_OUT;

  _7_segment_driver_main main_1 (
    .in_1(DISP_0), .out_6(main_1_out_6), .out_7(main_1_out_7), .out_8(main_1_out_8));  // open: out_2, out_3, out_4, out_5
  Clock clock_1 (.out(CLK));
  Button button_1 (.out(PB_1));
  Button button_2 (.out(PB_2));
  _7_segment_driver_main main_2 (
    .in_1(DISP_1), .out_2(main_2_out_2), .out_3(main_2_out_3), .out_4(main_2_out_4), .out_5(main_2_out_5));  // open: out_6, out_7, out_8
  _7_segment_driver_main main_3 (
    .in_1(DISP_0), .out_2(main_3_out_2), .out_3(main_3_out_3), .out_4(main_3_out_4), .out_5(main_3_out_5));  // open: out_6, out_7, out_8
  _7_Segment_Display u_7_segment_display_1 (
    .g(main_3_out_5), .f(main_3_out_4), .a(main_3_out_3), .b(main_3_out_2), .e(main_1_out_8),
    .d(main_1_out_7), .c(main_1_out_6));  // open: dp
  _7_segment_driver_main main_4 (
    .in_1(DISP_1), .out_6(main_4_out_6), .out_7(main_4_out_7), .out_8(main_4_out_8));  // open: out_2, out_3, out_4, out_5
  _7_segment_driver_main main_5 (
    .in_1(DISP_2), .out_2(main_5_out_2), .out_3(main_5_out_3), .out_4(main_5_out_4), .out_5(main_5_out_5));  // open: out_6, out_7, out_8
  _7_Segment_Display u_7_segment_display_2 (
    .g(main_5_out_5), .f(main_5_out_4), .a(main_5_out_3), .b(main_5_out_2), .e(main_6_out_8),
    .d(main_6_out_7), .c(main_6_out_6));  // open: dp
  _7_Segment_Display u_7_segment_display_3 (
    .g(main_2_out_5), .f(main_2_out_4), .a(main_2_out_3), .b(main_2_out_2), .e(main_4_out_8),
    .d(main_4_out_7), .c(main_4_out_6));  // open: dp
  _7_segment_driver_main main_6 (
    .in_1(DISP_2), .out_6(main_6_out_6), .out_7(main_6_out_7), .out_8(main_6_out_8));  // open: out_2, out_3, out_4, out_5
  _7_segment_driver_main main_7 (
    .in_1(DISP_3), .out_2(main_7_out_2), .out_3(main_7_out_3), .out_4(main_7_out_4), .out_5(main_7_out_5));  // open: out_6, out_7, out_8
  _7_Segment_Display u_7_segment_display_4 (
    .g(main_7_out_5), .f(main_7_out_4), .a(main_7_out_3), .b(main_7_out_2), .e(main_8_out_8),
    .d(main_8_out_7), .c(main_8_out_6));  // open: dp
  _7_segment_driver_main main_8 (
    .in_1(DISP_3), .out_6(main_8_out_6), .out_7(main_8_out_7), .out_8(main_8_out_8));  // open: out_2, out_3, out_4, out_5
  input_thing input_thing_1 (.BTN(PB_1), .CS(CS), .OUT(input_thing_1_out), .CLK(CLK), .IN(Pin_1), .ADDR_0(ADDR_0));
  input_thing input_thing_2 (.BTN(PB_2), .CS(CS), .CLK(CLK), .IN(Pin_2), .ADDR_0(ADDR_0));  // open: OUT
  _16_bit_register u_16_bit_register_1 (
    .IN(DATA_OUT), .LD(_7_SEG_LD), .CLK(CLK), .OUT({DISP_3, DISP_2, DISP_1, DISP_0}));
  Decoder #(.select(2), .disabled(0)) decoder_1 (.sel({2{ADDR_0}}), .en(and_1_out));  // open: out0, out1, out2, out3
  and and_1 (and_1_out, ADDR_OUT[15], ADDR_OUT[14], ADDR_OUT[13], ADDR_OUT[12], ADDR_OUT[11], ADDR_OUT[10], ADDR_OUT[9], undriven, ADDR_OUT[7], ADDR_OUT[6], ADDR_OUT[5], ADDR_OUT[4], not_1_out, not_2_out, 1'b1, 1'b1);
  not not_1 (not_1_out, ADDR_OUT[3]);
  not not_2 (not_2_out, ADDR_OUT[2]);
  Multiplexer #(.width(16), .enable("false")) multiplexer_1 (
    .in0(DATA_IN), .in1(input_thing_1_out), .out(multiplexer_1_out), .sel(CS));
  and and_2 (CS, ADDR_OUT[15], ADDR_OUT[14], ADDR_OUT[13], ADDR_OUT[12], ADDR_OUT[11], ADDR_OUT[10], ADDR_OUT[9], undriven_2, ADDR_OUT[7], ADDR_OUT[6], ADDR_OUT[5], ADDR_OUT[4], not_5_out, not_3_out, not_4_out, 1'b1);
  and and_3 (_7_SEG_LD, ADDR_OUT[15], ADDR_OUT[14], ADDR_OUT[13], ADDR_OUT[12], ADDR_OUT[11], ADDR_OUT[10], ADDR_OUT[9], undriven_3, ADDR_OUT[7], ADDR_OUT[6], ADDR_OUT[5], ADDR_OUT[4], not_7_out, ADDR_OUT[2], not_8_out, not_6_out);
  RAM #(.addrWidth(16), .dataWidth(16), .bus("separate")) ram_1 (
    .addr({ADDR_OUT, {2{ADDR_0}}}), .din(DATA_OUT), .data(DATA_IN), .str(MEMLD), .clk(CLK));  // open: sel, ld, clr
  Bird_CPU bird_cpu_1 (
    .DATA_IN(multiplexer_1_out), .CLK(CLK), .MEMLD(MEMLD), .ADDR_OUT({ADDR_OUT, {2{ADDR_0}}}),
    .DATA_OUT(DATA_OUT));
  not not_3 (not_3_out, ADDR_OUT[2]);
  not not_4 (not_4_out, ADDR_0);
  not not_5 (not_5_out, ADDR_OUT[3]);
  not not_6 (not_6_out, ADDR_0);
  not not_7 (not_7_out, ADDR_OUT[3]);
  not not_8 (not_8_out, ADDR_0);

  // Other names for the same wires on the sheet: ADDR_OUT[1:0] = {2{ADDR_0}}

  // Notes on the sheet:
  //   FFF0
  //   FFF1
  //   FFF2
  //   FFF3
  //   FFF0
  //   FFF1
  //   FFF2
  //   FFF3
endmodule

module input_thing (
  input  [15:0] IN,
  input  BTN,
  input  CLK,
  input  CS,
  input  ADDR_0,
  output [15:0] OUT
);

  wire and_1_out, and_2_out, and_3_out, not_1_out;
  wire [15:0] n16_bit_register_1_out;
  wire [15:15] s_r_ff_1_q;

  not not_1 (not_1_out, s_r_ff_1_q[15]);
  and and_1 (and_1_out, not_1_out, BTN);
  and and_2 (and_2_out, and_3_out, s_r_ff_1_q[15]);
  and and_3 (and_3_out, CS, ADDR_0);
  S_R_Flip_Flop s_r_ff_1 (.S(and_1_out), .clk(CLK), .R(and_2_out), .Q(s_r_ff_1_q[15]));  // open: Qn, preset, reset, en
  _16_bit_register u_16_bit_register_1 (.IN(IN), .LD(and_1_out), .CLK(CLK), .OUT(n16_bit_register_1_out));
  Multiplexer #(.width(16), .enable("false")) multiplexer_1 (
    .in0(n16_bit_register_1_out), .in1({s_r_ff_1_q[15], {15{1'b0}}}), .out(OUT), .sel(ADDR_0));
endmodule
