// Logisim project vertebrate.circ as structural Verilog: 16 circuits, main circuit Vertebrate_CPU
module Register_Bank (
  input  REG_LOAD,
  input  [2:0] REG_SELECT,
  input  [15:0] IN,
  input  ZFLD,
  input  Z,
  input  FLAGLD,
  input  STI,
  input  CLI,
  input  SP_plus_plus,
  input  SP_minus_minus,
  input  CLK,
  output [15:0] OUT_0,
  output [15:0] OUT_1,
  output [15:0] OUT_2,
  output [15:0] OUT_3,
  output [15:0] OUT_4,
  output [15:0] OUT_5,
  output IF,
  output ZF,
  output [15:0] OUT_6,
  output [15:0] OUT_7
);

  wire decoder_1_out0, decoder_1_out1, decoder_1_out2, decoder_1_out3, decoder_1_out4, decoder_1_out5,
       decoder_1_out6, decoder_1_out7;

  Decoder #(.select(3), .disabled(0)) decoder_1 (
    .out0(decoder_1_out0), .out1(decoder_1_out1), .out2(decoder_1_out2), .out3(decoder_1_out3),
    .out4(decoder_1_out4), .out5(decoder_1_out5), .out6(decoder_1_out6), .out7(decoder_1_out7),
    .sel(REG_SELECT), .en(REG_LOAD));
  _16_bit_register u_16_bit_register_1 (.IN(IN), .LD(decoder_1_out0), .CLK(CLK), .OUT(OUT_0));
  _16_bit_register u_16_bit_register_2 (.IN(IN), .LD(decoder_1_out1), .CLK(CLK), .OUT(OUT_1));
  _16_bit_register u_16_bit_register_3 (.IN(IN), .LD(decoder_1_out2), .CLK(CLK), .OUT(OUT_2));
  _16_bit_register u_16_bit_register_4 (.IN(IN), .LD(decoder_1_out3), .CLK(CLK), .OUT(OUT_3));
  _16_bit_register u_16_bit_register_5 (.IN(IN), .LD(decoder_1_out4), .CLK(CLK), .OUT(OUT_4));
  _16_bit_register u_16_bit_register_6 (.IN(IN), .LD(decoder_1_out5), .CLK(CLK), .OUT(OUT_5));
  stack_register stack_register_1 (
    .IN_DATA(IN), .out_6(OUT_7), .SP_plus_plus(SP_plus_plus), .SP_minus_minus(SP_minus_minus),
    .LD(decoder_1_out7), .CLK(CLK));
  flag_reg flag_reg_1 (
    .CLK(CLK), .CLI(CLI), .STI(STI), .REGLD(decoder_1_out6), .FLAGLD(FLAGLD), .Z(Z), .ZFLD(ZFLD), .IF(IF),
    .ZF(ZF), .OUT(OUT_6), .IN(IN));

  // Other names for the same wires on the sheet: IN_DATA[15:0] = IN
endmodule

module ALU (
  input  [15:0] IN_0,
  input  [15:0] IN_1,
  input  [5:0] ALUOP,
  output [15:0] RESULT,
  output ZF
);

  wire [15:0] adder_1_out, adder_2_out, and_1_out, Bitwise_Or_out, Bitwise_Xor_out, multiplexer_1_out,
       not_1_out, subtractor_1_out, subtractor_2_out;

  Adder #(.width(16)) adder_1 (.a(IN_0), .b(IN_1), .out(adder_1_out));  // open: cin, cout
  Subtractor #(.width(16)) subtractor_1 (.a(IN_0), .b(IN_1), .out(subtractor_1_out));  // open: bin, bout
  assign and_1_out = IN_0 & IN_1;  // AND_Gate and_1, 16 bits wide
  assign Bitwise_Or_out = IN_0 | IN_1;  // OR_Gate Bitwise_Or, 16 bits wide
  assign Bitwise_Xor_out = IN_0 ^ IN_1;  // XOR_Gate Bitwise_Xor, 16 bits wide
  assign not_1_out = ~IN_1;  // NOT_Gate not_1, 16 bits wide
  Adder #(.width(16)) adder_2 (.a(IN_1), .b(16'h1), .out(adder_2_out));  // open: cin, cout
  Subtractor #(.width(16)) subtractor_2 (.a(IN_1), .b(16'h1), .out(subtractor_2_out));  // open: bin, bout
  Multiplexer #(.select(3), .width(16), .enable("false")) multiplexer_1 (
    .in0(not_1_out), .in1(IN_1), .in2(adder_2_out), .in3(subtractor_2_out), .out(multiplexer_1_out),
    .sel({1'b0, ALUOP[1:0]}));  // open: in4, in5, in6, in7
  Multiplexer #(.select(3), .width(16), .enable("false")) multiplexer_2 (
    .in0(adder_1_out), .in1(subtractor_1_out), .in2(and_1_out), .in3(Bitwise_Or_out), .in4(Bitwise_Xor_out),
    .in7(multiplexer_1_out), .out(RESULT), .sel(ALUOP[5:3]));  // open: in5, in6
  nor nor_1 (ZF, RESULT[0], RESULT[1], RESULT[2], RESULT[3], RESULT[4], RESULT[5], RESULT[6], RESULT[7], RESULT[8], RESULT[9], RESULT[10], RESULT[11], RESULT[12], RESULT[13], RESULT[14], RESULT[15]);
endmodule

module Control_Unit (
  input  [3:0] OPCID,
  input  ZF,
  input  INT,
  input  INTFLAG,
  input  CLK,
  output IRLD,
  output MEMLD,
  output MUX,
  output ZFLD,
  output REGLD,
  output [1:0] ARMUX,
  output PCINC,
  output PCLD,
  output SP_minus_minus,
  output SP_plus_plus,
  output PCMUX,
  output [1:0] DATAMUX,
  output STI,
  output CLI,
  output INTLD,
  output INTACK,
  output FLAGLD
);

  wire and_2_out, and_3_out, FETCH, undriven;
  wire [1:1] and_1_out;
  wire [3:0] multiplexer_2_out;
  wire [4:0] multiplexer_1_out, multiplexer_3_out, n5_bit_register_1_out, NEXT_ADDR;

  and and_1 (and_1_out[1], ~OPCID[0], ~OPCID[1], OPCID[2], ~OPCID[3]);  // AND_Gate
  and and_2 (and_2_out, ~NEXT_ADDR[0], ~NEXT_ADDR[1], ~NEXT_ADDR[2], ~NEXT_ADDR[3], ~NEXT_ADDR[4]);  // AND_Gate
  Multiplexer #(.width(5), .enable("false")) multiplexer_1 (
    .in0(NEXT_ADDR), .in1({1'b0, multiplexer_2_out}), .out(multiplexer_1_out), .sel(FETCH));
  and and_3 (and_3_out, INT, INTFLAG, and_2_out, undriven);
  Multiplexer #(.select(2), .width(4), .disabled(0), .enable("false")) multiplexer_2 (
    .in0(OPCID), .in1(OPCID), .in2(4'b0100), .in3(4'b0101), .out(multiplexer_2_out), .sel({and_1_out[1], ZF}));
  Multiplexer #(.width(5), .enable("false")) multiplexer_3 (
    .in0(multiplexer_1_out), .in1(5'b10011), .out(multiplexer_3_out), .sel(and_3_out));
  _5_bit_register u_5_bit_register_1 (.IN(multiplexer_3_out), .LD(1'b1), .CLK(CLK), .OUT(n5_bit_register_1_out));
  ROM #(.addrWidth(5), .dataWidth(25)) rom_1 (
    .addr(n5_bit_register_1_out),
    .data({FETCH, FLAGLD, INTACK, INTLD, CLI, STI, DATAMUX, PCMUX, SP_plus_plus, SP_minus_minus, PCLD, PCINC, ARMUX, REGLD, ZFLD, MUX, MEMLD, IRLD, NEXT_ADDR}));  // open: sel

  // Other names for the same wires on the sheet: OPCODE[3:0] = OPCID

  // Notes on the sheet:
  //   contents of rom_1 (hex, n*v repeats v):
  //   1001020 1280 680 440 1000 2000 0 300 4840 8011 248c5 8012 80000 100000 800f 8890 812800 a80 12896
  //   124854 640855 12c00 1000
endmodule

module Program_Counter (
  input  PCMUX,
  input  [15:0] INSTRUCTION,
  input  PCINC,
  input  PCLD,
  input  CLK,
  input  [15:0] MEM_ADDR,
  input  [1:0] ARMUX,
  input  [15:0] STACK_POINTER,
  input  [15:0] INT_RESULT,
  output [15:0] PC_VAL,
  output [15:0] ADDR
);

  wire [15:0] adder_1_out, multiplexer_1_out;

  Adder #(.width(16)) adder_1 (.a(PC_VAL), .b(INSTRUCTION), .out(adder_1_out));  // open: cin, cout
  Multiplexer #(.width(16), .enable("false")) multiplexer_1 (
    .in0(adder_1_out), .in1(INSTRUCTION), .out(multiplexer_1_out), .sel(PCMUX));
  Counter counter_1 (.IN(multiplexer_1_out), .PCINC(PCINC), .PCLD(PCLD), .CLK(CLK), .OUT(PC_VAL));
  Multiplexer #(.select(2), .width(16), .enable("false")) multiplexer_2 (
    .in0(PC_VAL), .in1(MEM_ADDR), .in2(STACK_POINTER), .in3(INT_RESULT), .out(ADDR), .sel(ARMUX));
endmodule

module _1_bit_register (
  input  DATA_IN,
  input  CLK,
  input  LOAD,
  output DATA_OUT
);

  wire not_1_out;

  not not_1 (not_1_out, DATA_IN);
  S_R_Flip_Flop s_r_ff_1 (.S(DATA_IN), .clk(CLK), .R(not_1_out), .Q(DATA_OUT), .en(LOAD));  // open: Qn, preset, reset
endmodule

module _12_bit_register (
  input  [11:0] IN,
  input  LD,
  input  CLK,
  output [11:0] OUT
);

  _3_bit_register u_3_bit_register_1 (.IN(IN[2:0]), .CLK(CLK), .LD(LD), .OUT(OUT[2:0]));
  _3_bit_register u_3_bit_register_2 (.IN(IN[5:3]), .CLK(CLK), .LD(LD), .OUT(OUT[5:3]));
  _3_bit_register u_3_bit_register_3 (.IN(IN[8:6]), .CLK(CLK), .LD(LD), .OUT(OUT[8:6]));
  _3_bit_register u_3_bit_register_4 (.IN(IN[11:9]), .CLK(CLK), .LD(LD), .OUT(OUT[11:9]));
endmodule

module _16_bit_register (
  input  [15:0] IN,
  input  LD,
  input  CLK,
  output [15:0] OUT
);

  _4_bit_register u_4_bit_register_1 (.IN(IN[3:0]), .LD(LD), .CLK(CLK), .OUT(OUT[3:0]));
  _4_bit_register u_4_bit_register_2 (.IN(IN[7:4]), .LD(LD), .CLK(CLK), .OUT(OUT[7:4]));
  _4_bit_register u_4_bit_register_3 (.IN(IN[11:8]), .LD(LD), .CLK(CLK), .OUT(OUT[11:8]));
  _4_bit_register u_4_bit_register_4 (.IN(IN[15:12]), .LD(LD), .CLK(CLK), .OUT(OUT[15:12]));
endmodule

module _3_bit_register (
  input  [2:0] IN,
  input  CLK,
  input  LD,
  output [2:0] OUT
);

  _1_bit_register u_1_bit_register_1 (.DATA_IN(IN[0]), .CLK(CLK), .LOAD(LD), .DATA_OUT(OUT[0]));
  _1_bit_register u_1_bit_register_2 (.DATA_IN(IN[1]), .CLK(CLK), .LOAD(LD), .DATA_OUT(OUT[1]));
  _1_bit_register u_1_bit_register_3 (.DATA_IN(IN[2]), .CLK(CLK), .LOAD(LD), .DATA_OUT(OUT[2]));
endmodule

module _4_bit_register (
  input  [3:0] IN,
  input  LD,
  input  CLK,
  output [3:0] OUT
);

  _1_bit_register u_1_bit_register_1 (.DATA_IN(IN[0]), .CLK(CLK), .LOAD(LD), .DATA_OUT(OUT[0]));
  _1_bit_register u_1_bit_register_2 (.DATA_IN(IN[1]), .CLK(CLK), .LOAD(LD), .DATA_OUT(OUT[1]));
  _1_bit_register u_1_bit_register_3 (.DATA_IN(IN[2]), .CLK(CLK), .LOAD(LD), .DATA_OUT(OUT[2]));
  _1_bit_register u_1_bit_register_4 (.DATA_IN(IN[3]), .CLK(CLK), .LOAD(LD), .DATA_OUT(OUT[3]));
endmodule

module Instructor_Register (
  input  [11:0] IN,
  input  CLK,
  input  LD,
  output [11:0] OUT,
  output [2:0] DST,
  output [2:0] SRC2,
  output [5:0] ALUOP,
  output [2:0] SRC1
);

  _12_bit_register u_12_bit_register_1 (.IN(IN), .LD(LD), .CLK(CLK), .OUT({ALUOP, OUT[5:3], DST}));

  assign {OUT[11:6], OUT[2:0]} = {ALUOP, DST};
  assign SRC1 = ALUOP[2:0];
  assign SRC2 = OUT[5:3];
endmodule

module Counter (
  input  [15:0] IN,
  input  PCINC,
  input  PCLD,
  input  CLK,
  output [15:0] OUT
);

  wire Bitwise_Or_out;
  wire [15:0] adder_1_out, multiplexer_1_out;

  Adder #(.width(16)) adder_1 (.a(OUT), .b(16'h1), .out(adder_1_out));  // open: cin, cout
  Multiplexer #(.width(16), .enable("false")) multiplexer_1 (
    .in0(IN), .in1(adder_1_out), .out(multiplexer_1_out), .sel(PCINC));
  or Bitwise_Or (Bitwise_Or_out, PCINC, PCLD);
  _16_bit_register u_16_bit_register_1 (.IN(multiplexer_1_out), .LD(Bitwise_Or_out), .CLK(CLK), .OUT(OUT));
endmodule

module stack_register (
  input  [15:0] IN_DATA,
  input  SP_plus_plus,
  input  SP_minus_minus,
  input  LD,
  input  CLK,
  output [15:0] out_6
);

  wire Bitwise_Or_2_out, Bitwise_Or_out;
  wire [15:0] adder_1_out, multiplexer_1_out, multiplexer_2_out, subtractor_1_out;

  Adder #(.width(16)) adder_1 (.a(out_6), .b(16'h1), .out(adder_1_out));  // open: cin, cout
  Subtractor #(.width(16)) subtractor_1 (.a(out_6), .b(16'h1), .out(subtractor_1_out));  // open: bin, bout
  or Bitwise_Or (Bitwise_Or_out, SP_plus_plus, SP_minus_minus);
  Multiplexer #(.select(2), .width(16), .enable("false")) multiplexer_1 (
    .in1(adder_1_out), .in2(subtractor_1_out), .out(multiplexer_1_out), .sel({SP_minus_minus, SP_plus_plus}));  // open: in0, in3
  Multiplexer #(.width(16), .disabled(0), .enable("false")) multiplexer_2 (
    .in0(IN_DATA), .in1(multiplexer_1_out), .out(multiplexer_2_out), .sel(Bitwise_Or_out));
  or Bitwise_Or_2 (Bitwise_Or_2_out, Bitwise_Or_out, LD);
  _16_bit_register u_16_bit_register_1 (.IN(multiplexer_2_out), .LD(Bitwise_Or_2_out), .CLK(CLK), .OUT(out_6));
endmodule

module Vertebrate_CPU (
  input  [15:0] DATA_IN,
  input  CLK,
  input  INT,
  output MEMLD,
  output INTACK,
  output [15:0] ADDR_OUT,
  output [15:0] DATA_OUT
);

  wire CLI, FLAGLD, INTFLAG, INTLD, IRLD, MUX, PCINC, PCLD, PCMUX, REGLD, SP_minus_minus, SP_plus_plus, STI,
       Z, ZF, ZFLD;
  wire [1:0] ARMUX, DATAMUX;
  wire [2:0] REG_1, REG_2, REG_3;
  wire [5:0] ALUOP;
  wire [15:0] adder_1_out, ALU_AOUT, ALU_DOUT, ALU_RESULT, FLAG_REGISTER, INT_RES, multiplexer_1_out, PCVAL,
       register_bank_1_out_0, register_bank_1_out_1, register_bank_1_out_2, register_bank_1_out_3,
       register_bank_1_out_4, register_bank_1_out_5, STACK_POINTER;

  Multiplexer #(.width(16), .enable("false")) multiplexer_1 (
    .in0(ALU_RESULT), .in1(DATA_IN), .out(multiplexer_1_out), .sel(MUX));
  Register_Bank register_bank_1 (
    .REG_SELECT(REG_1), .CLK(CLK), .OUT_1(register_bank_1_out_1), .OUT_0(register_bank_1_out_0),
    .OUT_2(register_bank_1_out_2), .OUT_3(register_bank_1_out_3), .OUT_4(register_bank_1_out_4),
    .OUT_5(register_bank_1_out_5), .OUT_7(STACK_POINTER), .REG_LOAD(REGLD), .IN(multiplexer_1_out),
    .SP_plus_plus(SP_plus_plus), .SP_minus_minus(SP_minus_minus), .CLI(CLI), .FLAGLD(FLAGLD), .Z(Z),
    .IF(INTFLAG), .ZF(ZF), .STI(STI), .ZFLD(ZFLD), .OUT_6(FLAG_REGISTER));
  Adder #(.width(16)) adder_1 (.a(DATA_IN), .b(16'h7f0), .out(adder_1_out));  // open: cin, cout
  _16_bit_register u_16_bit_register_1 (.IN(adder_1_out), .LD(INTLD), .CLK(CLK), .OUT(INT_RES));
  Multiplexer #(.select(3), .width(16), .enable("false")) multiplexer_2 (
    .in0(register_bank_1_out_0), .in1(register_bank_1_out_1), .in2(register_bank_1_out_2),
    .in3(register_bank_1_out_3), .in4(register_bank_1_out_4), .in5(register_bank_1_out_5),
    .in6(FLAG_REGISTER), .in7(STACK_POINTER), .out(ALU_DOUT), .sel(REG_2));
  Instructor_Register instructor_register_1 (
    .IN(DATA_IN[11:0]), .CLK(CLK), .LD(IRLD), .DST(REG_1), .SRC2(REG_3), .SRC1(REG_2), .ALUOP(ALUOP));  // open: OUT
  ALU alu_1 (.IN_0(ALU_DOUT), .IN_1(ALU_AOUT), .RESULT(ALU_RESULT), .ZF(Z), .ALUOP(ALUOP));
  Multiplexer #(.select(3), .width(16), .enable("false")) multiplexer_3 (
    .in0(register_bank_1_out_0), .in1(register_bank_1_out_1), .in2(register_bank_1_out_2),
    .in3(register_bank_1_out_3), .in4(register_bank_1_out_4), .in5(register_bank_1_out_5),
    .in6(FLAG_REGISTER), .in7(STACK_POINTER), .out(ALU_AOUT), .sel(REG_3));
  Control_Unit control_unit_1 (
    .OPCID(DATA_IN[15:12]), .ZF(ZF), .CLK(CLK), .MEMLD(MEMLD), .MUX(MUX), .ZFLD(ZFLD), .REGLD(REGLD),
    .PCINC(PCINC), .PCLD(PCLD), .DATAMUX(DATAMUX), .ARMUX(ARMUX), .SP_plus_plus(SP_plus_plus),
    .SP_minus_minus(SP_minus_minus), .PCMUX(PCMUX), .INTLD(INTLD), .FLAGLD(FLAGLD), .CLI(CLI), .STI(STI),
    .IRLD(IRLD), .INT(INT), .INTFLAG(INTFLAG), .INTACK(INTACK));
  Program_Counter program_counter_1 (
    .PCINC(PCINC), .PCLD(PCLD), .CLK(CLK), .MEM_ADDR(ALU_AOUT), .ARMUX(ARMUX), .ADDR(ADDR_OUT),
    .STACK_POINTER(STACK_POINTER), .PCMUX(PCMUX), .INSTRUCTION(DATA_IN), .PC_VAL(PCVAL), .INT_RESULT(INT_RES));
  Multiplexer #(.select(2), .width(16), .enable("false")) multiplexer_4 (
    .in0(ALU_DOUT), .in1(PCVAL), .in2(FLAG_REGISTER), .out(DATA_OUT), .sel(DATAMUX));  // open: in3

  // Other names for the same wires on the sheet: INSTRUCTION[15:0] = DATA_IN; INSTRUCTION_BODY[11:0] = DATA_IN[11:0];
  //   OPCODE[3:0] = DATA_IN[15:12]; PCOUT[15:0] = ADDR_OUT
endmodule

module _5_bit_register (
  input  [4:0] IN,
  input  LD,
  input  CLK,
  output [4:0] OUT
);

  _1_bit_register u_1_bit_register_1 (.DATA_IN(IN[0]), .CLK(CLK), .LOAD(LD), .DATA_OUT(OUT[0]));
  _1_bit_register u_1_bit_register_2 (.DATA_IN(IN[1]), .CLK(CLK), .LOAD(LD), .DATA_OUT(OUT[1]));
  _1_bit_register u_1_bit_register_3 (.DATA_IN(IN[2]), .CLK(CLK), .LOAD(LD), .DATA_OUT(OUT[2]));
  _1_bit_register u_1_bit_register_4 (.DATA_IN(IN[3]), .CLK(CLK), .LOAD(LD), .DATA_OUT(OUT[3]));
  _1_bit_register u_1_bit_register_5 (.DATA_IN(IN[4]), .CLK(CLK), .LOAD(LD), .DATA_OUT(OUT[4]));
endmodule

module test (
  input  INT,
  output INTACK,
  output [15:0] ADDR_OUT,
  output [15:0] DATA_OUT
);

  wire CLI, CLK, FLAGLD, INTFLAG, INTLD, IRLD, MEMLD, MUX, PCINC, PCLD, PCMUX, REGLD, SP_minus_minus,
       SP_plus_plus, STI, Z, ZF, ZFLD;
  wire [1:0] ARMUX, DATAMUX;
  wire [2:0] REG_1, REG_2, REG_3;
  wire [5:0] ALUOP;
  wire [15:0] adder_1_out, ALU_AOUT, ALU_DOUT, ALU_RESULT, FLAG_REGISTER, INSTRUCTION, INT_RES,
       multiplexer_1_out, PCVAL, register_bank_1_out_0, register_bank_1_out_1, register_bank_1_out_2,
       register_bank_1_out_3, register_bank_1_out_4, register_bank_1_out_5, STACK_POINTER;

  Clock clock_1 (.out(CLK));
  RAM #(.addrWidth(16), .dataWidth(16), .bus("separate")) ram_1 (
    .addr(ADDR_OUT), .din(DATA_OUT), .data(INSTRUCTION), .str(MEMLD), .clk(CLK));  // open: sel, ld, clr
  Multiplexer #(.width(16), .enable("false")) multiplexer_1 (
    .in0(ALU_RESULT), .in1(INSTRUCTION), .out(multiplexer_1_out), .sel(MUX));
  Register_Bank register_bank_1 (
    .REG_SELECT(REG_1), .CLK(CLK), .OUT_1(register_bank_1_out_1), .OUT_0(register_bank_1_out_0),
    .OUT_2(register_bank_1_out_2), .OUT_3(register_bank_1_out_3), .OUT_4(register_bank_1_out_4),
    .OUT_5(register_bank_1_out_5), .OUT_7(STACK_POINTER), .REG_LOAD(REGLD), .IN(multiplexer_1_out),
    .SP_plus_plus(SP_plus_plus), .SP_minus_minus(SP_minus_minus), .CLI(CLI), .FLAGLD(FLAGLD), .Z(Z),
    .IF(INTFLAG), .ZF(ZF), .STI(STI), .ZFLD(ZFLD), .OUT_6(FLAG_REGISTER));
  Adder #(.width(16)) adder_1 (.a(INSTRUCTION), .b(16'h7f0), .out(adder_1_out));  // open: cin, cout
  Multiplexer #(.select(3), .width(16), .enable("false")) multiplexer_2 (
    .in0(register_bank_1_out_0), .in1(register_bank_1_out_1), .in2(register_bank_1_out_2),
    .in3(register_bank_1_out_3), .in4(register_bank_1_out_4), .in5(register_bank_1_out_5),
    .in6(FLAG_REGISTER), .in7(STACK_POINTER), .out(ALU_DOUT), .sel(REG_2));
  Instructor_Register instructor_register_1 (
    .IN(INSTRUCTION[11:0]), .CLK(CLK), .LD(IRLD), .DST(REG_1), .SRC2(REG_3), .SRC1(REG_2), .ALUOP(ALUOP));  // open: OUT
  _16_bit_register u_16_bit_register_1 (.IN(adder_1_out), .LD(INTLD), .CLK(CLK), .OUT(INT_RES));
  ALU alu_1 (.IN_0(ALU_DOUT), .IN_1(ALU_AOUT), .RESULT(ALU_RESULT), .ZF(Z), .ALUOP(ALUOP));
  Multiplexer #(.select(3), .width(16), .enable("false")) multiplexer_3 (
    .in0(register_bank_1_out_0), .in1(register_bank_1_out_1), .in2(register_bank_1_out_2),
    .in3(register_bank_1_out_3), .in4(register_bank_1_out_4), .in5(register_bank_1_out_5),
    .in6(FLAG_REGISTER), .in7(STACK_POINTER), .out(ALU_AOUT), .sel(REG_3));
  Control_Unit control_unit_1 (
    .OPCID(INSTRUCTION[15:12]), .ZF(ZF), .CLK(CLK), .MEMLD(MEMLD), .MUX(MUX), .ZFLD(ZFLD), .REGLD(REGLD),
    .PCINC(PCINC), .PCLD(PCLD), .DATAMUX(DATAMUX), .ARMUX(ARMUX), .SP_plus_plus(SP_plus_plus),
    .SP_minus_minus(SP_minus_minus), .PCMUX(PCMUX), .INTLD(INTLD), .FLAGLD(FLAGLD), .CLI(CLI), .STI(STI),
    .IRLD(IRLD), .INT(INT), .INTFLAG(INTFLAG), .INTACK(INTACK));
  Program_Counter program_counter_1 (
    .PCINC(PCINC), .PCLD(PCLD), .CLK(CLK), .MEM_ADDR(ALU_AOUT), .ARMUX(ARMUX), .ADDR(ADDR_OUT),
    .STACK_POINTER(STACK_POINTER), .PCMUX(PCMUX), .INSTRUCTION(INSTRUCTION), .PC_VAL(PCVAL),
    .INT_RESULT(INT_RES));
  Multiplexer #(.select(2), .width(16), .enable("false")) multiplexer_4 (
    .in0(ALU_DOUT), .in1(PCVAL), .in2(FLAG_REGISTER), .out(DATA_OUT), .sel(DATAMUX));  // open: in3

  // Other names for the same wires on the sheet: DATA[15:0] = DATA_OUT; INSTRUCTION_BODY[11:0] = INSTRUCTION[11:0];
  //   OPCODE[3:0] = INSTRUCTION[15:12]; ADDR[15:0] = ADDR_OUT; PCOUT[15:0] = ADDR_OUT
endmodule

module flag_reg (
  input  [15:0] IN,
  input  CLK,
  input  STI,
  input  CLI,
  input  Z,
  input  REGLD,
  input  ZFLD,
  input  FLAGLD,
  output [15:0] OUT,
  output ZF,
  output IF
);

  wire and_1_out, and_2_out, and_3_out, and_4_out, and_5_out, and_6_out, and_7_out, Bitwise_Or_2_out,
       Bitwise_Or_3_out, Bitwise_Or_4_out, Bitwise_Or_5_out, Bitwise_Or_6_out, Bitwise_Or_out, undriven;

  buf Bitwise_Or (Bitwise_Or_out, STI);  // OR_Gate
  and and_1 (and_1_out, REGLD, FLAGLD);
  and and_2 (and_2_out, ~REGLD, FLAGLD);  // AND_Gate
  or Bitwise_Or_2 (Bitwise_Or_2_out, Bitwise_Or_out, and_1_out);
  or Bitwise_Or_3 (Bitwise_Or_3_out, CLI, and_2_out);
  S_R_Flip_Flop s_r_ff_1 (
    .S(Bitwise_Or_2_out), .clk(CLK), .R(Bitwise_Or_3_out), .Q(IF));  // open: Qn, preset, reset, en
  and and_3 (and_3_out, undriven, REGLD);
  or Bitwise_Or_4 (Bitwise_Or_4_out, and_3_out, and_4_out);
  and and_4 (and_4_out, REGLD, FLAGLD);
  and and_5 (and_5_out, ~REGLD, FLAGLD);  // AND_Gate
  or Bitwise_Or_5 (Bitwise_Or_5_out, Bitwise_Or_4_out, and_6_out);
  and and_6 (and_6_out, ZFLD, Z);
  or Bitwise_Or_6 (Bitwise_Or_6_out, and_5_out, and_7_out);
  and and_7 (and_7_out, ZFLD, ~Z);  // AND_Gate
  S_R_Flip_Flop s_r_ff_2 (
    .S(Bitwise_Or_5_out), .clk(CLK), .R(Bitwise_Or_6_out), .Q(OUT[0]));  // open: Qn, preset, reset, en

  assign OUT[15:1] = {{14{1'b0}}, IF};
  assign ZF = OUT[0];
endmodule
