// Logisim project homework_1.circ as structural Verilog: 9 circuits, main circuit reptile_8
module reptile_8 (
);

  wire ARMUX, clk, IRLD, MEMLD, MUX, PCINC, PCLD, REGLD, undriven_8, zf, ZFLD;
  wire [2:0] DST, SRC_1, SRC_2;
  wire [3:0] opcode, undriven_9, undriven_10, undriven_11, undriven_12;
  wire [5:0] ALUOP;
  wire [11:0] adder_1_out, ADDR, IR_IN, mem_address, multiplexer_1_out, program_counter_1_addr_out;
  wire [15:0] data_in, Dout, undriven, undriven_2, undriven_3, undriven_4, undriven_5, undriven_6,
       undriven_7, undriven_13;
  wire [15:12] multiplexer_3_out;

  Clock clock_1 (.out(clk));
  register_bank register_bank_1 (
    .Reg_Select(DST), .REG_LD(REGLD), .Data_in(data_in),
    .d_out_0({undriven_12, undriven_11, undriven_10, undriven_9}), .d_out_1(undriven), .d_out_2(undriven_2),
    .d_out_3(undriven_3), .d_out_4(undriven_4), .d_out_5(undriven_5), .d_out_6(undriven_6),
    .d_out_0_2(undriven_7), .CLK(clk));
  Adder #(.width(12)) adder_1 (.a(program_counter_1_addr_out), .b(ADDR), .out(adder_1_out));  // open: cin, cout
  program_counter program_counter_1 (
    .CLK(clk), .ADDR_IN(adder_1_out), .PC_LOAD(PCLD), .INCREMENT(PCINC), .ADDR_OUT(program_counter_1_addr_out));
  Multiplexer #(.width(12)) multiplexer_1 (
    .in0(program_counter_1_addr_out), .in1(mem_address), .out(multiplexer_1_out), .sel(ARMUX));  // open: en
  Hex_Digit_Display hex_digit_display_1 (.value(undriven_11));  // open: dp
  Hex_Digit_Display hex_digit_display_2 (.value(undriven_12));  // open: dp
  Hex_Digit_Display hex_digit_display_3 (.value(undriven_10));  // open: dp
  register register_1 (.DATA_IN(undriven_8), .CLK(clk), .LOAD(ZFLD), .DATA__OUT(zf));
  RAM #(.addrWidth(12), .dataWidth(16), .bus("separate")) ram_1 (
    .addr(multiplexer_1_out), .din(Dout), .data({opcode, IR_IN}), .str(MEMLD), .clk(clk));  // open: sel, ld, clr
  Hex_Digit_Display hex_digit_display_4 (.value(undriven_9));  // open: dp
  Multiplexer #(.select(3), .width(16)) multiplexer_2 (
    .in0({undriven_12, undriven_11, undriven_10, undriven_9}), .in1(undriven), .in2(undriven_2),
    .in3(undriven_3), .in4(undriven_4), .in5(undriven_5), .in6(undriven_6), .in7(undriven_7), .out(Dout),
    .sel(SRC_2));  // open: en
  ALU alu_1 (
    .Din1(Dout), .Din2({multiplexer_3_out, mem_address}), .in_1(undriven_8), .result(undriven_13),
    .ALU_OP(ALUOP));
  Multiplexer #(.select(3), .width(16)) multiplexer_3 (
    .in0({undriven_12, undriven_11, undriven_10, undriven_9}), .in1(undriven), .in2(undriven_2),
    .in3(undriven_3), .in4(undriven_4), .in5(undriven_5), .in6(undriven_6), .in7(undriven_7),
    .out({multiplexer_3_out, mem_address}), .sel(SRC_1));  // open: en
  Multiplexer #(.width(16)) multiplexer_4 (
    .in0(undriven_13), .in1({opcode, IR_IN}), .out(data_in), .sel(MUX));  // open: en
  IR ir_1 (
    .D_IN(IR_IN), .CLK(clk), .LOAD(IRLD), .dst(DST), .src_1(SRC_1), .src_2(SRC_2), .ALU_CODE(ALUOP),
    .ADDR(ADDR));
  circuit_bank circuit_bank_1 (
    .LOAD(1'b1), .ZF(zf), .OPCODE(opcode), .IRLD(IRLD), .MEMLD(MEMLD), .MUX(MUX), .ZFLD(ZFLD), .REGLD(REGLD),
    .ARMUX(ARMUX), .PCINC(PCINC), .PCLD(PCLD), .clk(clk));

  // Other names for the same wires on the sheet: whole_instruction[15:0] = {opcode, IR_IN}
endmodule

module circuit_bank (
  input  LOAD,
  input  clk,
  input  ZF,
  input  [3:0] OPCODE,
  output IRLD,
  output MEMLD,
  output MUX,
  output ZFLD,
  output REGLD,
  output ARMUX,
  output PCINC,
  output PCLD
);

  wire [1:1] and_1_out;
  wire [3:0] multiplexer_1_out, multiplexer_2_out, register_1_q, undriven;
  wire [8:8] rom_1_data;

  Register #(.width(4)) register_1 (.D(multiplexer_1_out), .en(LOAD), .Q(register_1_q), .clk(clk));  // open: clr
  and and_1 (and_1_out[1], ~undriven[0], ~undriven[1], undriven[2], ~undriven[3]);  // AND_Gate
  Multiplexer #(.width(4)) multiplexer_1 (
    .in0(4'b0000), .in1(multiplexer_2_out), .out(multiplexer_1_out), .sel(rom_1_data[8]));  // open: en
  Multiplexer #(.select(2), .width(4)) multiplexer_2 (
    .in0(OPCODE), .in1(undriven), .in2(4'b0000), .in3(4'b1101), .out(multiplexer_2_out),
    .sel({and_1_out[1], ZF}));  // open: en
  ROM #(.addrWidth(4), .dataWidth(9)) rom_1 (
    .addr(register_1_q), .data({rom_1_data[8], PCLD, PCINC, ARMUX, REGLD, ZFLD, MUX, MEMLD, IRLD}));  // open: sel

  // Notes on the sheet:
  //   contents of rom_1 (hex, n*v repeats v):
  //   141 54 34 22 0 80 0 18
endmodule

module register_bank (
  input  [15:0] d_out_0,
  input  [15:0] d_out_1,
  input  [15:0] d_out_2,
  input  [15:0] d_out_3,
  input  [15:0] d_out_4,
  input  [2:0] Reg_Select,
  input  [15:0] d_out_5,
  input  [15:0] d_out_6,
  input  REG_LD,
  input  [15:0] d_out_0_2,
  input  [15:0] Data_in,
  input  CLK
);

  wire and_1_out, and_2_out, and_3_out, and_4_out, and_5_out, and_6_out, and_7_out, and_8_out,
       decoder_1_out0, decoder_1_out1, decoder_1_out2, decoder_1_out3, decoder_1_out4, decoder_1_out5,
       decoder_1_out6, decoder_1_out7;

  Decoder #(.select(3)) decoder_1 (
    .out0(decoder_1_out0), .out1(decoder_1_out1), .out2(decoder_1_out2), .out3(decoder_1_out3),
    .out4(decoder_1_out4), .out5(decoder_1_out5), .out6(decoder_1_out6), .out7(decoder_1_out7),
    .sel(Reg_Select));  // open: en
  and and_1 (and_1_out, decoder_1_out0, REG_LD);
  and and_2 (and_2_out, decoder_1_out1, REG_LD);
  and and_3 (and_3_out, decoder_1_out2, REG_LD);
  and and_4 (and_4_out, decoder_1_out3, REG_LD);
  and and_5 (and_5_out, decoder_1_out4, REG_LD);
  and and_6 (and_6_out, decoder_1_out5, REG_LD);
  and and_7 (and_7_out, decoder_1_out6, REG_LD);
  and and_8 (and_8_out, decoder_1_out7, REG_LD);
  _16_bit_register u_16_bit_register_1 (.DATA_IN(Data_in), .CLK(and_1_out), .LOAD(CLK), .DATA_OUT(d_out_0));
  _16_bit_register u_16_bit_register_2 (.DATA_IN(Data_in), .CLK(and_2_out), .LOAD(CLK), .DATA_OUT(d_out_1));
  _16_bit_register u_16_bit_register_3 (.DATA_IN(Data_in), .CLK(and_3_out), .LOAD(CLK), .DATA_OUT(d_out_2));
  _16_bit_register u_16_bit_register_4 (.DATA_IN(Data_in), .CLK(and_4_out), .LOAD(CLK), .DATA_OUT(d_out_3));
  _16_bit_register u_16_bit_register_5 (.DATA_IN(Data_in), .CLK(and_5_out), .LOAD(CLK), .DATA_OUT(d_out_4));
  _16_bit_register u_16_bit_register_6 (.DATA_IN(Data_in), .CLK(and_6_out), .LOAD(CLK), .DATA_OUT(d_out_5));
  _16_bit_register u_16_bit_register_7 (.DATA_IN(Data_in), .CLK(and_7_out), .LOAD(CLK), .DATA_OUT(d_out_6));
  _16_bit_register u_16_bit_register_8 (.DATA_IN(Data_in), .CLK(and_8_out), .LOAD(CLK), .DATA_OUT(d_out_0_2));
endmodule

module register (
  input  DATA_IN,
  input  CLK,
  input  LOAD,
  output DATA__OUT
);

  wire not_1_out;

  not not_1 (not_1_out, DATA_IN);
  S_R_Flip_Flop s_r_ff_1 (.S(DATA_IN), .clk(CLK), .R(not_1_out), .Q(DATA__OUT), .en(LOAD));  // open: Qn, preset, reset
endmodule

module program_counter (
  input  CLK,
  input  [11:0] ADDR_IN,
  input  PC_LOAD,
  input  INCREMENT,
  output [11:0] ADDR_OUT
);

  wire or_1_out;
  wire [11:0] adder_1_out;

  or or_1 (or_1_out, PC_LOAD, INCREMENT);
  _12_bit_register u_12_bit_register_1 (.CLK(CLK), .LOAD(or_1_out), .DATA_OUT(ADDR_OUT));  // open: DATA_IN
  Adder #(.width(12)) adder_1 (.a(ADDR_OUT), .b(12'h1), .out(adder_1_out));  // open: cin, cout
  Multiplexer #(.width(12)) multiplexer_1 (.in0(ADDR_IN), .in1(adder_1_out), .sel(INCREMENT));  // open: out, en
endmodule

module _16_bit_register (
  input  [15:0] DATA_IN,
  input  CLK,
  input  LOAD,
  output [15:0] DATA_OUT
);

  register register_1 (.DATA_IN(DATA_IN[0]), .CLK(CLK), .LOAD(LOAD), .DATA__OUT(DATA_OUT[0]));
  register register_2 (.DATA_IN(DATA_IN[1]), .CLK(CLK), .LOAD(LOAD), .DATA__OUT(DATA_OUT[1]));
  register register_3 (.DATA_IN(DATA_IN[2]), .CLK(CLK), .LOAD(LOAD), .DATA__OUT(DATA_OUT[2]));
  register register_4 (.DATA_IN(DATA_IN[3]), .CLK(CLK), .LOAD(LOAD), .DATA__OUT(DATA_OUT[3]));
  register register_5 (.DATA_IN(DATA_IN[4]), .CLK(CLK), .LOAD(LOAD), .DATA__OUT(DATA_OUT[4]));
  register register_6 (.DATA_IN(DATA_IN[5]), .CLK(CLK), .LOAD(LOAD), .DATA__OUT(DATA_OUT[5]));
  register register_7 (.DATA_IN(DATA_IN[6]), .CLK(CLK), .LOAD(LOAD), .DATA__OUT(DATA_OUT[6]));
  register register_8 (.DATA_IN(DATA_IN[7]), .CLK(CLK), .LOAD(LOAD), .DATA__OUT(DATA_OUT[7]));
  register register_9 (.DATA_IN(DATA_IN[8]), .CLK(CLK), .LOAD(LOAD), .DATA__OUT(DATA_OUT[8]));
  register register_10 (.DATA_IN(DATA_IN[9]), .CLK(CLK), .LOAD(LOAD), .DATA__OUT(DATA_OUT[9]));
  register register_11 (.DATA_IN(DATA_IN[10]), .CLK(CLK), .LOAD(LOAD), .DATA__OUT(DATA_OUT[10]));
  register register_12 (.DATA_IN(DATA_IN[11]), .CLK(CLK), .LOAD(LOAD), .DATA__OUT(DATA_OUT[11]));
  register register_13 (.DATA_IN(DATA_IN[12]), .CLK(CLK), .LOAD(LOAD), .DATA__OUT(DATA_OUT[12]));
  register register_14 (.DATA_IN(DATA_IN[13]), .CLK(CLK), .LOAD(LOAD), .DATA__OUT(DATA_OUT[13]));
  register register_15 (.DATA_IN(DATA_IN[14]), .CLK(CLK), .LOAD(LOAD), .DATA__OUT(DATA_OUT[14]));
  register register_16 (.DATA_IN(DATA_IN[15]), .CLK(CLK), .LOAD(LOAD), .DATA__OUT(DATA_OUT[15]));
endmodule

module ALU (
  input  in_1,
  input  [15:0] Din1,
  input  [15:0] Din2,
  input  [15:0] result,
  input  [5:0] ALU_OP
);

  wire [15:0] adder_1_out, adder_2_out, and_1_out, multiplexer_1_out, not_1_out, or_1_out, subtractor_1_out,
       subtractor_2_out, xor_1_out;

  Adder #(.width(16)) adder_1 (.a(Din1), .b(Din2), .out(adder_1_out));  // open: cin, cout
  Subtractor #(.width(16)) subtractor_1 (.a(Din1), .b(Din2), .out(subtractor_1_out));  // open: bin, bout
  assign and_1_out = Din1 & Din2;  // AND_Gate and_1, 16 bits wide
  assign or_1_out = Din1 | Din2;  // OR_Gate or_1, 16 bits wide
  assign xor_1_out = Din1 ^ Din2;  // XOR_Gate xor_1, 16 bits wide
  assign not_1_out = ~Din2;  // NOT_Gate not_1, 16 bits wide
  Adder #(.width(16)) adder_2 (.a(Din2), .b(16'h1), .out(adder_2_out));  // open: cin, cout
  Subtractor #(.width(16)) subtractor_2 (.a(Din2), .b(16'h1), .out(subtractor_2_out));  // open: bin, bout
  Multiplexer #(.select(3), .width(16)) multiplexer_1 (
    .in0(not_1_out), .in1(Din2), .in2(adder_2_out), .in3(subtractor_2_out), .out(multiplexer_1_out),
    .sel(ALU_OP[2:0]));  // open: in4, in5, in6, in7, en
  Multiplexer #(.select(3), .width(16)) multiplexer_2 (
    .in0(adder_1_out), .in1(subtractor_1_out), .in2(and_1_out), .in3(or_1_out), .in4(xor_1_out),
    .in7(multiplexer_1_out), .out(result), .sel(ALU_OP[5:3]));  // open: in5, in6, en
  nor ZF (in_1, result[0], result[1], result[2], result[3], result[4], result[5], result[6], result[7], result[8], result[9], result[10], result[11], result[12], result[13], result[14], result[15]);
endmodule

module _12_bit_register (
  input  [11:0] DATA_IN,
  input  CLK,
  input  LOAD,
  output [11:0] DATA_OUT
);

  register register_1 (.DATA_IN(DATA_IN[0]), .CLK(CLK), .LOAD(LOAD), .DATA__OUT(DATA_OUT[0]));
  register register_2 (.DATA_IN(DATA_IN[1]), .CLK(CLK), .LOAD(LOAD), .DATA__OUT(DATA_OUT[1]));
  register register_3 (.DATA_IN(DATA_IN[2]), .CLK(CLK), .LOAD(LOAD), .DATA__OUT(DATA_OUT[2]));
  register register_4 (.DATA_IN(DATA_IN[3]), .CLK(CLK), .LOAD(LOAD), .DATA__OUT(DATA_OUT[3]));
  register register_5 (.DATA_IN(DATA_IN[4]), .CLK(CLK), .LOAD(LOAD), .DATA__OUT(DATA_OUT[4]));
  register register_6 (.DATA_IN(DATA_IN[5]), .CLK(CLK), .LOAD(LOAD), .DATA__OUT(DATA_OUT[5]));
  register register_7 (.DATA_IN(DATA_IN[6]), .CLK(CLK), .LOAD(LOAD), .DATA__OUT(DATA_OUT[6]));
  register register_8 (.DATA_IN(DATA_IN[7]), .CLK(CLK), .LOAD(LOAD), .DATA__OUT(DATA_OUT[7]));
  register register_9 (.DATA_IN(DATA_IN[8]), .CLK(CLK), .LOAD(LOAD), .DATA__OUT(DATA_OUT[8]));
  register register_10 (.DATA_IN(DATA_IN[9]), .CLK(CLK), .LOAD(LOAD), .DATA__OUT(DATA_OUT[9]));
  register register_11 (.DATA_IN(DATA_IN[10]), .CLK(CLK), .LOAD(LOAD), .DATA__OUT(DATA_OUT[10]));
  register register_12 (.DATA_IN(DATA_IN[11]), .CLK(CLK), .LOAD(LOAD), .DATA__OUT(DATA_OUT[11]));
endmodule

module IR (
  input  [11:0] D_IN,
  input  CLK,
  input  LOAD,
  output [2:0] dst,
  output [2:0] src_1,
  output [2:0] src_2,
  output [5:0] ALU_CODE,
  output [11:0] ADDR
);

  _12_bit_register u_12_bit_register_1 (.DATA_IN(D_IN), .CLK(CLK), .LOAD(LOAD), .DATA_OUT(ADDR));

  assign ALU_CODE = ADDR[11:6];
  assign dst = ADDR[2:0];
  assign src_1 = ADDR[5:3];
  assign src_2 = ADDR[8:6];
endmodule
